// Logisim project project.circ as structural Verilog
module _1_bit_LU (
  input  A,
  input  B,
  input  [2:0] in_3,
  output out_4
);

  wire nand_1_out, nor_1_out, not_1_out, xor_1_out;

  nand nand_1 (nand_1_out, A, B);
  nor nor_1 (nor_1_out, A, B);
  xor xor_1 (xor_1_out, A, B);
  not not_1 (not_1_out, A);
  Multiplexer #(.select(3), .enable("false")) multiplexer_1 (
    .in0(nand_1_out), .in1(nor_1_out), .in2(not_1_out), .in7(xor_1_out), .out(out_4), .sel(in_3));  // open: in3, in4, in5, in6
endmodule

module _2_bit_Lu (
  input  A,
  input  B,
  input  A_2,
  input  B_2,
  input  [1:0] in_5,
  output out_6,
  output out_7
);

  wire and_1_out, and_2_out, not_1_out, not_2_out, or_1_out, or_2_out, xor_1_out, xor_2_out;

  and and_1 (and_1_out, A, B);
  or or_1 (or_1_out, A, B);
  xor xor_1 (xor_1_out, A, B);
  not not_1 (not_1_out, A);
  and and_2 (and_2_out, A_2, B_2);
  or or_2 (or_2_out, A_2, B_2);
  xor xor_2 (xor_2_out, A_2, B_2);
  not not_2 (not_2_out, A_2);
  Multiplexer #(.select(2), .enable("false")) multiplexer_1 (
    .in0(and_1_out), .in1(or_1_out), .in2(xor_1_out), .in3(not_1_out), .out(out_6), .sel(in_5));
  Multiplexer #(.select(2), .enable("false")) multiplexer_2 (
    .in0(and_2_out), .in1(or_2_out), .in2(xor_2_out), .in3(not_2_out), .out(out_7), .sel(in_5));
endmodule

module _16bit_lu (
  input  [15:0] B,
  input  [15:0] A,
  input  [2:0] in_3,
  output [15:0] out_4
);

  _4_bit_lu u_4_bit_lu_1 (
    .out_10(out_4[0]), .out_11(out_4[1]), .out_12(out_4[2]), .out_13(out_4[3]), .A(A[0]), .A_2(A[1]),
    .A_3(A[2]), .A_4(A[3]), .B(B[0]), .B_2(B[1]), .B_3(B[2]), .B_4(B[3]), .in_9(in_3));
  _4_bit_lu u_4_bit_lu_2 (
    .out_10(out_4[4]), .out_11(out_4[5]), .out_12(out_4[6]), .out_13(out_4[7]), .A(A[4]), .A_2(A[5]),
    .A_3(A[6]), .A_4(A[7]), .B(B[4]), .B_2(B[5]), .B_3(B[6]), .B_4(B[7]), .in_9(in_3));
  _4_bit_lu u_4_bit_lu_3 (
    .out_10(out_4[8]), .out_11(out_4[9]), .out_12(out_4[10]), .out_13(out_4[11]), .A(A[8]), .A_2(A[9]),
    .A_3(A[10]), .A_4(A[11]), .B(B[8]), .B_2(B[9]), .B_3(B[10]), .B_4(B[11]), .in_9(in_3));
  _4_bit_lu u_4_bit_lu_4 (
    .out_10(out_4[12]), .out_11(out_4[13]), .out_12(out_4[14]), .out_13(out_4[15]), .A(A[12]), .A_2(A[13]),
    .A_3(A[14]), .A_4(A[15]), .B(B[12]), .B_2(B[13]), .B_3(B[14]), .B_4(B[15]), .in_9(in_3));
endmodule

module Extra (
  input  [3:0] in_1,
  input  [3:0] in_2,
  input  [1:0] in_3,
  output F1,
  output F2,
  output F3,
  output F4
);

  wire [2:2] undriven;

  _1_bit_LU u_1_bit_lu_1 (.in_3({undriven[2], in_3}), .out_4(F1), .A(in_2[0]), .B(in_1[0]));
  _1_bit_LU u_1_bit_lu_2 (.in_3({undriven[2], in_3}), .out_4(F2), .A(in_2[1]), .B(in_1[1]));
  _1_bit_LU u_1_bit_lu_3 (.in_3({undriven[2], in_3}), .out_4(F3), .A(in_2[2]), .B(in_1[2]));
  _1_bit_LU u_1_bit_lu_4 (.in_3({undriven[2], in_3}), .out_4(F4), .A(in_2[3]), .B(in_1[3]));
  // Pins of 2 and 3 bits meet at {undriven[2], in_3}
endmodule

module _4_bit_lu (
  input  A,
  input  B,
  input  A_2,
  input  B_2,
  input  A_3,
  input  B_3,
  input  A_4,
  input  B_4,
  input  [2:0] in_9,
  output out_10,
  output out_11,
  output out_12,
  output out_13
);

  wire nand_1_out, nand_2_out, nand_3_out, nand_4_out, nor_1_out, nor_2_out, nor_3_out, nor_4_out, not_1_out,
       not_2_out, not_3_out, not_4_out, xor_1_out, xor_2_out, xor_3_out, xor_4_out;

  nand nand_1 (nand_1_out, A, B);
  nor nor_1 (nor_1_out, A, B);
  xor xor_1 (xor_1_out, A, B);
  not not_1 (not_1_out, A);
  nand nand_2 (nand_2_out, A_2, B_2);
  nor nor_2 (nor_2_out, A_2, B_2);
  xor xor_2 (xor_2_out, A_2, B_2);
  not not_2 (not_2_out, A_2);
  nand nand_3 (nand_3_out, A_3, B_3);
  nor nor_3 (nor_3_out, A_3, B_3);
  xor xor_3 (xor_3_out, A_3, B_3);
  not not_3 (not_3_out, A_3);
  nand nand_4 (nand_4_out, A_4, B_4);
  nor nor_4 (nor_4_out, A_4, B_4);
  xor xor_4 (xor_4_out, A_4, B_4);
  not not_4 (not_4_out, A_4);
  Multiplexer #(.select(3), .enable("false")) multiplexer_1 (
    .in0(nand_1_out), .in1(nor_1_out), .in2(not_1_out), .in7(xor_1_out), .out(out_10), .sel(in_9));  // open: in3, in4, in5, in6
  Multiplexer #(.select(3), .enable("false")) multiplexer_2 (
    .in0(nand_2_out), .in1(nor_2_out), .in2(not_2_out), .in7(xor_2_out), .out(out_11), .sel(in_9));  // open: in3, in4, in5, in6
  Multiplexer #(.select(3), .enable("false")) multiplexer_3 (
    .in0(nand_3_out), .in1(nor_3_out), .in2(not_3_out), .in7(xor_3_out), .out(out_12), .sel(in_9));  // open: in3, in4, in5, in6
  Multiplexer #(.select(3), .enable("false")) multiplexer_4 (
    .in0(nand_4_out), .in1(nor_4_out), .in2(not_4_out), .in7(xor_4_out), .out(out_13), .sel(in_9));  // open: in3, in4, in5, in6
endmodule

module _1_bit_AU (
  input  A,
  input  B,
  input  in_3,
  input  [2:0] in_4,
  input  in_5,
  output out_6,
  output out_7,
  output out_8
);

  wire n1_bit_adder_1_s, n1_bit_adder_2_s, not_1_out;

  not not_1 (not_1_out, B);
  _1_bit_adder u_1_bit_adder_1 (.S(n1_bit_adder_1_s), .Cout(out_7), .A(A), .B(B), .Cin(in_3));
  _1_bit_adder u_1_bit_adder_2 (.S(n1_bit_adder_2_s), .Cout(out_8), .A(A), .B(not_1_out), .Cin(in_5));
  Multiplexer #(.select(3), .enable("false")) multiplexer_1 (
    .in2(n1_bit_adder_1_s), .in6(n1_bit_adder_2_s), .out(out_6), .sel(in_4));  // open: in0, in1, in3, in4, in5, in7
endmodule

module _1_bit_adder (
  input  A,
  input  B,
  input  Cin,
  output S,
  output Cout
);

  wire and_1_out, and_2_out, xor_1_out;

  xor xor_1 (xor_1_out, A, B);
  xor xor_2 (S, xor_1_out, Cin);
  and and_1 (and_1_out, Cin, xor_1_out);
  and and_2 (and_2_out, A, B);
  or or_1 (Cout, and_1_out, and_2_out);
endmodule

module _4_bit_Au (
  input  in_1,
  input  in_2,
  input  B3,
  input  B2,
  input  B1,
  input  B0,
  input  A3,
  input  A2,
  input  A1,
  input  A0,
  input  [2:0] in_11,
  output D3,
  output D2,
  output D1,
  output D0,
  output out_16,
  output out_17
);

  wire n1_bit_au_1_out_7, n1_bit_au_1_out_8, n1_bit_au_2_out_7, n1_bit_au_2_out_8, n1_bit_au_3_out_7,
       n1_bit_au_3_out_8;

  _1_bit_AU u_1_bit_au_1 (
    .in_4(in_11), .A(A0), .B(B0), .in_3(in_1), .out_7(n1_bit_au_1_out_7), .in_5(in_2),
    .out_8(n1_bit_au_1_out_8), .out_6(D0));
  _1_bit_AU u_1_bit_au_2 (
    .in_4(in_11), .A(A1), .B(B1), .in_3(n1_bit_au_1_out_7), .out_7(n1_bit_au_2_out_7),
    .in_5(n1_bit_au_1_out_8), .out_8(n1_bit_au_2_out_8), .out_6(D1));
  _1_bit_AU u_1_bit_au_3 (
    .in_4(in_11), .A(A2), .B(B2), .in_3(n1_bit_au_2_out_7), .out_7(n1_bit_au_3_out_7),
    .in_5(n1_bit_au_2_out_8), .out_8(n1_bit_au_3_out_8), .out_6(D2));
  _1_bit_AU u_1_bit_au_4 (
    .in_4(in_11), .A(A3), .B(B3), .in_3(n1_bit_au_3_out_7), .out_7(out_16), .in_5(n1_bit_au_3_out_8),
    .out_8(out_17), .out_6(D3));
endmodule

module _16_bit_AU (
  input  in_1,
  input  in_2,
  input  [15:0] A,
  input  [15:0] B,
  input  [2:0] in_5,
  output [15:0] out_6,
  output out_7,
  output out_8
);

  wire n4_bit_au_1_out_16, n4_bit_au_1_out_17, n4_bit_au_2_out_16, n4_bit_au_2_out_17, n4_bit_au_3_out_16,
       n4_bit_au_3_out_17;

  _4_bit_Au u_4_bit_au_1 (
    .B3(B[3]), .B2(B[2]), .B1(B[1]), .B0(B[0]), .A3(A[3]), .A2(A[2]), .A1(A[1]), .A0(A[0]), .in_2(in_2),
    .D0(out_6[0]), .D1(out_6[1]), .D2(out_6[2]), .D3(out_6[3]), .in_1(in_1), .in_11(in_5),
    .out_16(n4_bit_au_1_out_16), .out_17(n4_bit_au_1_out_17));
  _4_bit_Au u_4_bit_au_2 (
    .B3(B[7]), .B2(B[6]), .B1(B[5]), .B0(B[4]), .A3(A[7]), .A2(A[6]), .A1(A[5]), .A0(A[4]),
    .in_2(n4_bit_au_1_out_17), .D0(out_6[4]), .D1(out_6[5]), .D2(out_6[6]), .D3(out_6[7]),
    .in_1(n4_bit_au_1_out_16), .in_11(in_5), .out_16(n4_bit_au_2_out_16), .out_17(n4_bit_au_2_out_17));
  _4_bit_Au u_4_bit_au_3 (
    .B3(A[11]), .B2(A[10]), .B1(A[9]), .B0(A[8]), .A3(B[11]), .A2(B[10]), .A1(B[9]), .A0(B[8]),
    .in_2(n4_bit_au_2_out_17), .D0(out_6[8]), .D1(out_6[9]), .D2(out_6[10]), .D3(out_6[11]),
    .in_1(n4_bit_au_2_out_16), .in_11(in_5), .out_16(n4_bit_au_3_out_16), .out_17(n4_bit_au_3_out_17));
  _4_bit_Au u_4_bit_au_4 (
    .B3(A[15]), .B2(A[14]), .B1(A[13]), .B0(A[12]), .A3(B[15]), .A2(B[14]), .A1(B[13]), .A0(B[12]),
    .in_2(n4_bit_au_3_out_17), .D0(out_6[12]), .D1(out_6[13]), .D2(out_6[14]), .D3(out_6[15]),
    .in_1(n4_bit_au_3_out_16), .in_11(in_5), .out_16(out_7), .out_17(out_8));
endmodule

module _4_bit_adder (
  input  Cin,
  input  A3,
  input  A2,
  input  A1,
  input  A0,
  input  B3,
  input  B2,
  input  B1,
  input  B0,
  output S0,
  output S1,
  output S2,
  output S3,
  output out_14
);

  wire n1_bit_adder_1_cout, n1_bit_adder_2_cout, n1_bit_adder_3_cout;

  _1_bit_adder u_1_bit_adder_1 (.S(S0), .Cout(n1_bit_adder_1_cout), .A(A0), .B(B0), .Cin(Cin));
  _1_bit_adder u_1_bit_adder_2 (.S(S1), .Cout(n1_bit_adder_2_cout), .A(A1), .B(B1), .Cin(n1_bit_adder_1_cout));
  _1_bit_adder u_1_bit_adder_3 (.S(S2), .Cout(n1_bit_adder_3_cout), .A(A2), .B(B2), .Cin(n1_bit_adder_2_cout));
  _1_bit_adder u_1_bit_adder_4 (.S(S3), .Cout(out_14), .A(A3), .B(B3), .Cin(n1_bit_adder_3_cout));
endmodule

module _4_bit_multiplier (
  input  B3,
  input  B2,
  input  B1,
  input  B0,
  input  A3,
  input  A2,
  input  A1,
  input  A0,
  output [7:0] out_9
);

  wire and_2_out, and_3_out, and_4_out, and_5_out, and_6_out, and_7_out, and_8_out, and_9_out, and_10_out,
       and_11_out, and_12_out, and_13_out, and_14_out, and_15_out, and_16_out, n4_bit_adder_1_out_14,
       n4_bit_adder_1_s1, n4_bit_adder_1_s2, n4_bit_adder_1_s3, n4_bit_adder_2_out_14, n4_bit_adder_2_s1,
       n4_bit_adder_2_s2, n4_bit_adder_2_s3;

  and and_1 (out_9[0], B0, A0);
  and and_2 (and_2_out, B1, A0);
  and and_3 (and_3_out, B2, A0);
  and and_4 (and_4_out, B3, A0);
  and and_5 (and_5_out, B0, A1);
  and and_6 (and_6_out, B1, A1);
  and and_7 (and_7_out, B2, A1);
  and and_8 (and_8_out, B3, A1);
  and and_9 (and_9_out, B0, A2);
  and and_10 (and_10_out, B1, A2);
  and and_11 (and_11_out, B2, A2);
  and and_12 (and_12_out, B3, A2);
  and and_13 (and_13_out, B0, A3);
  and and_14 (and_14_out, B1, A3);
  and and_15 (and_15_out, B2, A3);
  and and_16 (and_16_out, B3, A3);
  _4_bit_adder u_4_bit_adder_1 (
    .out_14(n4_bit_adder_1_out_14), .Cin(1'b0), .A2(and_7_out), .A1(and_6_out), .A0(and_5_out), .B3(1'b0),
    .B2(and_4_out), .B1(and_3_out), .B0(and_2_out), .A3(and_8_out), .S0(out_9[1]), .S1(n4_bit_adder_1_s1),
    .S3(n4_bit_adder_1_s3), .S2(n4_bit_adder_1_s2));
  _4_bit_adder u_4_bit_adder_2 (
    .out_14(n4_bit_adder_2_out_14), .Cin(1'b0), .A2(and_11_out), .A1(and_10_out), .A0(and_9_out),
    .B3(n4_bit_adder_1_out_14), .B2(n4_bit_adder_1_s3), .B1(n4_bit_adder_1_s2), .B0(n4_bit_adder_1_s1),
    .A3(and_12_out), .S0(out_9[2]), .S1(n4_bit_adder_2_s1), .S3(n4_bit_adder_2_s3), .S2(n4_bit_adder_2_s2));
  _4_bit_adder u_4_bit_adder_3 (
    .out_14(out_9[7]), .Cin(1'b0), .A2(and_15_out), .A1(and_14_out), .A0(and_13_out),
    .B3(n4_bit_adder_2_out_14), .B2(n4_bit_adder_2_s3), .B1(n4_bit_adder_2_s2), .B0(n4_bit_adder_2_s1),
    .A3(and_16_out), .S0(out_9[3]), .S1(out_9[4]), .S3(out_9[6]), .S2(out_9[5]));
  // Probe on out_9
endmodule

module _8_bit_multiplier (
  input  B7,
  input  B6,
  input  B5,
  input  B4,
  input  B3,
  input  B2,
  input  B1,
  input  B0,
  input  A7,
  input  A6,
  input  A5,
  input  A4,
  input  A3,
  input  A2,
  input  A1,
  input  A0,
  output [15:0] out_17
);

  wire and_2_out, and_3_out, and_4_out, and_5_out, and_6_out, and_7_out, and_8_out, and_9_out, and_10_out,
       and_11_out, and_12_out, and_13_out, and_14_out, and_15_out, and_16_out, and_17_out, and_18_out,
       and_19_out, and_20_out, and_21_out, and_22_out, and_23_out, and_24_out, and_25_out, and_26_out,
       and_27_out, and_28_out, and_29_out, and_30_out, and_31_out, and_32_out, and_33_out, and_34_out,
       and_35_out, and_36_out, and_37_out, and_38_out, and_39_out, and_40_out, and_41_out, and_42_out,
       and_43_out, and_44_out, and_45_out, and_46_out, and_47_out, and_48_out, and_49_out, and_50_out,
       and_51_out, and_52_out, and_53_out, and_54_out, and_55_out, and_56_out, and_57_out, and_58_out,
       and_59_out, and_60_out, and_61_out, and_62_out, and_63_out, and_64_out, n8_bit_adder_1_out_19,
       n8_bit_adder_1_out_20, n8_bit_adder_1_out_21, n8_bit_adder_1_out_22, n8_bit_adder_1_out_23,
       n8_bit_adder_1_out_24, n8_bit_adder_1_out_25, n8_bit_adder_1_out_26, n8_bit_adder_2_out_19,
       n8_bit_adder_2_out_20, n8_bit_adder_2_out_21, n8_bit_adder_2_out_22, n8_bit_adder_2_out_23,
       n8_bit_adder_2_out_24, n8_bit_adder_2_out_25, n8_bit_adder_2_out_26, n8_bit_adder_3_out_19,
       n8_bit_adder_3_out_20, n8_bit_adder_3_out_21, n8_bit_adder_3_out_22, n8_bit_adder_3_out_23,
       n8_bit_adder_3_out_24, n8_bit_adder_3_out_25, n8_bit_adder_3_out_26, n8_bit_adder_4_out_19,
       n8_bit_adder_4_out_20, n8_bit_adder_4_out_21, n8_bit_adder_4_out_22, n8_bit_adder_4_out_23,
       n8_bit_adder_4_out_24, n8_bit_adder_4_out_25, n8_bit_adder_4_out_26, n8_bit_adder_5_out_19,
       n8_bit_adder_5_out_20, n8_bit_adder_5_out_21, n8_bit_adder_5_out_22, n8_bit_adder_5_out_23,
       n8_bit_adder_5_out_24, n8_bit_adder_5_out_25, n8_bit_adder_5_out_26, n8_bit_adder_7_out_19,
       n8_bit_adder_7_out_20, n8_bit_adder_7_out_21, n8_bit_adder_7_out_22, n8_bit_adder_7_out_23,
       n8_bit_adder_7_out_24, n8_bit_adder_7_out_25, n8_bit_adder_7_out_26;

  and and_1 (out_17[0], B0, A0);
  and and_2 (and_2_out, B1, A0);
  and and_3 (and_3_out, B2, A0);
  and and_4 (and_4_out, B3, A0);
  and and_5 (and_5_out, B4, A0);
  and and_6 (and_6_out, B5, A0);
  and and_7 (and_7_out, B6, A0);
  and and_8 (and_8_out, B7, A0);
  and and_9 (and_9_out, B0, A1);
  and and_10 (and_10_out, B1, A1);
  and and_11 (and_11_out, B2, A1);
  and and_12 (and_12_out, B3, A1);
  and and_13 (and_13_out, B4, A1);
  and and_14 (and_14_out, B5, A1);
  and and_15 (and_15_out, B6, A1);
  and and_16 (and_16_out, B7, A1);
  and and_17 (and_17_out, B0, A2);
  and and_18 (and_18_out, B1, A2);
  and and_19 (and_19_out, B2, A2);
  and and_20 (and_20_out, B3, A2);
  and and_21 (and_21_out, B4, A2);
  and and_22 (and_22_out, B5, A2);
  and and_23 (and_23_out, B6, A2);
  and and_24 (and_24_out, B7, A2);
  and and_25 (and_25_out, B0, A3);
  and and_26 (and_26_out, B1, A3);
  and and_27 (and_27_out, B2, A3);
  and and_28 (and_28_out, B3, A3);
  and and_29 (and_29_out, B4, A3);
  and and_30 (and_30_out, B5, A3);
  and and_31 (and_31_out, B6, A3);
  and and_32 (and_32_out, B7, A3);
  and and_33 (and_33_out, B0, A4);
  and and_34 (and_34_out, B1, A4);
  and and_35 (and_35_out, B2, A4);
  and and_36 (and_36_out, B3, A4);
  and and_37 (and_37_out, B4, A4);
  and and_38 (and_38_out, B5, A4);
  and and_39 (and_39_out, B6, A4);
  and and_40 (and_40_out, B7, A4);
  and and_41 (and_41_out, B0, A5);
  and and_42 (and_42_out, B1, A5);
  and and_43 (and_43_out, B2, A5);
  and and_44 (and_44_out, B3, A5);
  and and_45 (and_45_out, B4, A5);
  and and_46 (and_46_out, B5, A5);
  and and_47 (and_47_out, B6, A5);
  and and_48 (and_48_out, B7, A5);
  and and_49 (and_49_out, B0, A6);
  and and_50 (and_50_out, B1, A6);
  and and_51 (and_51_out, B2, A6);
  and and_52 (and_52_out, B3, A6);
  and and_53 (and_53_out, B4, A6);
  and and_54 (and_54_out, B5, A6);
  and and_55 (and_55_out, B6, A6);
  and and_56 (and_56_out, B7, A6);
  and and_57 (and_57_out, B0, A7);
  and and_58 (and_58_out, B1, A7);
  and and_59 (and_59_out, B2, A7);
  and and_60 (and_60_out, B3, A7);
  and and_61 (and_61_out, B4, A7);
  and and_62 (and_62_out, B5, A7);
  and and_63 (and_63_out, B6, A7);
  and and_64 (and_64_out, B7, A7);
  _8_bit_adder u_8_bit_adder_1 (
    .out_18(out_17[1]), .out_19(n8_bit_adder_1_out_19), .out_20(n8_bit_adder_1_out_20),
    .out_21(n8_bit_adder_1_out_21), .out_22(n8_bit_adder_1_out_22), .out_23(n8_bit_adder_1_out_23),
    .out_24(n8_bit_adder_1_out_24), .out_25(n8_bit_adder_1_out_25), .out_26(n8_bit_adder_1_out_26),
    .B7(and_16_out), .B6(and_15_out), .B5(and_14_out), .B4(and_13_out), .B3(and_12_out), .B2(and_11_out),
    .B1(and_10_out), .B0(and_9_out), .A7(1'b0), .A6(and_8_out), .A5(and_7_out), .A4(and_6_out),
    .A3(and_5_out), .A2(and_4_out), .A1(and_3_out), .A0(and_2_out), .Cin(1'b0));
  _8_bit_adder u_8_bit_adder_2 (
    .out_18(out_17[3]), .out_19(n8_bit_adder_2_out_19), .out_20(n8_bit_adder_2_out_20),
    .out_21(n8_bit_adder_2_out_21), .out_22(n8_bit_adder_2_out_22), .out_23(n8_bit_adder_2_out_23),
    .out_24(n8_bit_adder_2_out_24), .out_25(n8_bit_adder_2_out_25), .out_26(n8_bit_adder_2_out_26),
    .B7(and_32_out), .B6(and_31_out), .B5(and_30_out), .B4(and_29_out), .B3(and_28_out), .B2(and_27_out),
    .B1(and_26_out), .B0(and_25_out), .A7(n8_bit_adder_7_out_26), .A6(n8_bit_adder_7_out_25),
    .A5(n8_bit_adder_7_out_24), .A4(n8_bit_adder_7_out_23), .A3(n8_bit_adder_7_out_22),
    .A2(n8_bit_adder_7_out_21), .A1(n8_bit_adder_7_out_20), .A0(n8_bit_adder_7_out_19), .Cin(1'b0));
  _8_bit_adder u_8_bit_adder_3 (
    .out_18(out_17[4]), .out_19(n8_bit_adder_3_out_19), .out_20(n8_bit_adder_3_out_20),
    .out_21(n8_bit_adder_3_out_21), .out_22(n8_bit_adder_3_out_22), .out_23(n8_bit_adder_3_out_23),
    .out_24(n8_bit_adder_3_out_24), .out_25(n8_bit_adder_3_out_25), .out_26(n8_bit_adder_3_out_26),
    .B7(and_40_out), .B6(and_39_out), .B5(and_38_out), .B4(and_37_out), .B3(and_36_out), .B2(and_35_out),
    .B1(and_34_out), .B0(and_33_out), .A7(n8_bit_adder_2_out_26), .A6(n8_bit_adder_2_out_25),
    .A5(n8_bit_adder_2_out_24), .A4(n8_bit_adder_2_out_23), .A3(n8_bit_adder_2_out_22),
    .A2(n8_bit_adder_2_out_21), .A1(n8_bit_adder_2_out_20), .A0(n8_bit_adder_2_out_19), .Cin(1'b0));
  _8_bit_adder u_8_bit_adder_4 (
    .out_18(out_17[5]), .out_19(n8_bit_adder_4_out_19), .out_20(n8_bit_adder_4_out_20),
    .out_21(n8_bit_adder_4_out_21), .out_22(n8_bit_adder_4_out_22), .out_23(n8_bit_adder_4_out_23),
    .out_24(n8_bit_adder_4_out_24), .out_25(n8_bit_adder_4_out_25), .out_26(n8_bit_adder_4_out_26),
    .B7(and_48_out), .B6(and_47_out), .B5(and_46_out), .B4(and_45_out), .B3(and_44_out), .B2(and_43_out),
    .B1(and_42_out), .B0(and_41_out), .A7(n8_bit_adder_3_out_26), .A6(n8_bit_adder_3_out_25),
    .A5(n8_bit_adder_3_out_24), .A4(n8_bit_adder_3_out_23), .A3(n8_bit_adder_3_out_22),
    .A2(n8_bit_adder_3_out_21), .A1(n8_bit_adder_3_out_20), .A0(n8_bit_adder_3_out_19), .Cin(1'b0));
  _8_bit_adder u_8_bit_adder_5 (
    .out_18(out_17[6]), .out_19(n8_bit_adder_5_out_19), .out_20(n8_bit_adder_5_out_20),
    .out_21(n8_bit_adder_5_out_21), .out_22(n8_bit_adder_5_out_22), .out_23(n8_bit_adder_5_out_23),
    .out_24(n8_bit_adder_5_out_24), .out_25(n8_bit_adder_5_out_25), .out_26(n8_bit_adder_5_out_26),
    .B7(and_56_out), .B6(and_55_out), .B5(and_54_out), .B4(and_53_out), .B3(and_52_out), .B2(and_51_out),
    .B1(and_50_out), .B0(and_49_out), .A7(n8_bit_adder_4_out_26), .A6(n8_bit_adder_4_out_25),
    .A5(n8_bit_adder_4_out_24), .A4(n8_bit_adder_4_out_23), .A3(n8_bit_adder_4_out_22),
    .A2(n8_bit_adder_4_out_21), .A1(n8_bit_adder_4_out_20), .A0(n8_bit_adder_4_out_19), .Cin(1'b0));
  _8_bit_adder u_8_bit_adder_6 (
    .out_18(out_17[7]), .out_19(out_17[8]), .out_20(out_17[9]), .out_21(out_17[10]), .out_22(out_17[11]),
    .out_23(out_17[12]), .out_24(out_17[13]), .out_25(out_17[14]), .out_26(out_17[15]), .B7(and_64_out),
    .B6(and_63_out), .B5(and_62_out), .B4(and_61_out), .B3(and_60_out), .B2(and_59_out), .B1(and_58_out),
    .B0(and_57_out), .A7(n8_bit_adder_5_out_26), .A6(n8_bit_adder_5_out_25), .A5(n8_bit_adder_5_out_24),
    .A4(n8_bit_adder_5_out_23), .A3(n8_bit_adder_5_out_22), .A2(n8_bit_adder_5_out_21),
    .A1(n8_bit_adder_5_out_20), .A0(n8_bit_adder_5_out_19), .Cin(1'b0));
  _8_bit_adder u_8_bit_adder_7 (
    .out_18(out_17[2]), .out_19(n8_bit_adder_7_out_19), .out_20(n8_bit_adder_7_out_20),
    .out_21(n8_bit_adder_7_out_21), .out_22(n8_bit_adder_7_out_22), .out_23(n8_bit_adder_7_out_23),
    .out_24(n8_bit_adder_7_out_24), .out_25(n8_bit_adder_7_out_25), .out_26(n8_bit_adder_7_out_26),
    .B7(and_24_out), .B6(and_23_out), .B5(and_22_out), .B4(and_21_out), .B3(and_20_out), .B2(and_19_out),
    .B1(and_18_out), .B0(and_17_out), .A7(n8_bit_adder_1_out_26), .A6(n8_bit_adder_1_out_25),
    .A5(n8_bit_adder_1_out_24), .A4(n8_bit_adder_1_out_23), .A3(n8_bit_adder_1_out_22),
    .A2(n8_bit_adder_1_out_21), .A1(n8_bit_adder_1_out_20), .A0(n8_bit_adder_1_out_19), .Cin(1'b0));
  // Probe on out_17
endmodule

module _8_bit_adder (
  input  B7,
  input  B6,
  input  B5,
  input  B4,
  input  B3,
  input  B2,
  input  B1,
  input  B0,
  input  A7,
  input  A6,
  input  A5,
  input  A4,
  input  A3,
  input  A2,
  input  A1,
  input  A0,
  input  Cin,
  output out_18,
  output out_19,
  output out_20,
  output out_21,
  output out_22,
  output out_23,
  output out_24,
  output out_25,
  output out_26
);

  wire n4_bit_adder_1_out_14;

  _4_bit_adder u_4_bit_adder_1 (
    .out_14(n4_bit_adder_1_out_14), .Cin(Cin), .A2(A2), .A1(A1), .A0(A0), .B3(B3), .B2(B2), .B1(B1), .B0(B0),
    .A3(A3), .S0(out_18), .S1(out_19), .S3(out_21), .S2(out_20));
  _4_bit_adder u_4_bit_adder_2 (
    .out_14(out_26), .Cin(n4_bit_adder_1_out_14), .A2(A6), .A1(A5), .A0(A4), .B3(B7), .B2(B6), .B1(B5),
    .B0(B4), .A3(A7), .S0(out_22), .S1(out_23), .S3(out_25), .S2(out_24));
endmodule

module _1_bit_Alu (
  input  A,
  input  B,
  input  Ain,
  input  Bin,
  input  Cin_add,
  input  Cin_sub,
  input  [2:0] in_7,
  output out_8,
  output Cout_add,
  output Cout_Sub
);

  wire and_1_out, comparator_1_lt, multiplexer_1_out, multiplexer_2_out, multiplier_1_out, n1_bit_adder_1_s,
       n1_bit_adder_2_s, not_1_out, not_2_out, or_1_out;

  not not_1 (not_1_out, A);
  Multiplexer #(.enable("false")) multiplexer_1 (.in0(B), .in1(not_2_out), .out(multiplexer_1_out), .sel(Bin));
  not not_2 (not_2_out, B);
  Multiplexer #(.enable("false")) multiplexer_2 (.in0(A), .in1(not_1_out), .out(multiplexer_2_out), .sel(Ain));
  and and_1 (and_1_out, multiplexer_2_out, multiplexer_1_out);
  or or_1 (or_1_out, multiplexer_2_out, multiplexer_1_out);
  Multiplier #(.width(1)) multiplier_1 (
    .a(multiplexer_2_out), .b(multiplexer_1_out), .out(multiplier_1_out));  // open: cin, cout
  Comparator #(.width(1)) comparator_1 (
    .a(multiplexer_2_out), .b(multiplexer_1_out), .lt(comparator_1_lt));  // open: gt, eq
  _1_bit_adder u_1_bit_adder_1 (
    .S(n1_bit_adder_1_s), .Cout(Cout_add), .A(multiplexer_2_out), .B(multiplexer_1_out), .Cin(Cin_add));
  _1_bit_adder u_1_bit_adder_2 (
    .S(n1_bit_adder_2_s), .Cout(Cout_Sub), .A(multiplexer_2_out), .B(multiplexer_1_out), .Cin(Cin_sub));
  Multiplexer #(.select(3), .enable("false")) multiplexer_3 (
    .in0(and_1_out), .in2(n1_bit_adder_1_s), .in3(multiplier_1_out), .in4(or_1_out), .in6(n1_bit_adder_2_s),
    .in7(comparator_1_lt), .out(out_8), .sel(in_7));  // open: in1, in5
endmodule

module Alu_con_in (
  input  F5,
  input  F4,
  input  F3,
  input  F2,
  input  F1,
  input  F0,
  input  OP0,
  input  OP1,
  output [2:0] out_9
);

  wire and_1_out, or_1_out;

  or or_1 (or_1_out, F3, F0);
  and and_1 (and_1_out, OP1, F1);
  and and_2 (out_9[2], OP1, or_1_out);
  or or_2 (out_9[0], OP0, and_1_out);
  or or_3 (out_9[1], ~OP1, ~F2);  // OR_Gate
endmodule

module _4_bit_Alu (
  input  [3:0] A,
  input  [3:0] B,
  input  Ain,
  input  Bin,
  input  Cin_a,
  input  Cin_s,
  input  [5:0] in_7,
  input  in_8,
  input  in_9,
  output O3,
  output O2,
  output O1,
  output O0,
  output out_14,
  output out_15
);

  wire n1_bit_alu_1_cout_add, n1_bit_alu_1_cout_sub, n1_bit_alu_2_cout_add, n1_bit_alu_2_cout_sub,
       n1_bit_alu_3_cout_add, n1_bit_alu_3_cout_sub;
  wire [2:0] alu_con_in_1_out_9;

  Alu_con_in alu_con_in_1 (
    .out_9(alu_con_in_1_out_9), .F5(in_7[5]), .F4(in_7[4]), .F3(in_7[3]), .F2(in_7[2]), .F1(in_7[1]),
    .F0(in_7[0]), .OP0(in_9), .OP1(in_8));
  _1_bit_Alu u_1_bit_alu_1 (
    .A(A[0]), .B(B[0]), .Ain(Ain), .Bin(Bin), .Cin_add(Cin_a), .Cin_sub(Cin_s), .out_8(O0),
    .Cout_add(n1_bit_alu_1_cout_add), .Cout_Sub(n1_bit_alu_1_cout_sub), .in_7(alu_con_in_1_out_9));
  _1_bit_Alu u_1_bit_alu_2 (
    .A(A[1]), .B(B[1]), .Ain(Ain), .Bin(Bin), .Cin_add(n1_bit_alu_1_cout_add),
    .Cin_sub(n1_bit_alu_1_cout_sub), .out_8(O1), .Cout_add(n1_bit_alu_2_cout_add),
    .Cout_Sub(n1_bit_alu_2_cout_sub), .in_7(alu_con_in_1_out_9));
  _1_bit_Alu u_1_bit_alu_3 (
    .A(A[2]), .B(B[2]), .Ain(Ain), .Bin(Bin), .Cin_add(n1_bit_alu_2_cout_add),
    .Cin_sub(n1_bit_alu_2_cout_sub), .out_8(O2), .Cout_add(n1_bit_alu_3_cout_add),
    .Cout_Sub(n1_bit_alu_3_cout_sub), .in_7(alu_con_in_1_out_9));
  _1_bit_Alu u_1_bit_alu_4 (
    .A(A[3]), .B(B[3]), .Ain(Ain), .Bin(Bin), .Cin_add(n1_bit_alu_3_cout_add),
    .Cin_sub(n1_bit_alu_3_cout_sub), .out_8(O3), .Cout_add(out_14), .Cout_Sub(out_15),
    .in_7(alu_con_in_1_out_9));
endmodule

module _16_bit_ALU (
  input  [5:0] in_1,
  input  in_2,
  input  in_3,
  input  in_4,
  input  in_5,
  input  Ain,
  input  Bin,
  input  [15:0] A,
  input  [15:0] B,
  output [15:0] out_10,
  output out_11,
  output out_12,
  output [2:0] out_13
);

  wire n4_bit_alu_1_out_14, n4_bit_alu_1_out_15, n4_bit_alu_2_out_14, n4_bit_alu_2_out_15,
       n4_bit_alu_3_out_14, n4_bit_alu_3_out_15;

  _4_bit_Alu u_4_bit_alu_1 (
    .out_14(n4_bit_alu_1_out_14), .out_15(n4_bit_alu_1_out_15), .in_7(in_1), .A(A[3:0]), .in_8(in_2),
    .B(B[3:0]), .in_9(in_3), .Ain(Ain), .Bin(Bin), .Cin_a(in_4), .Cin_s(in_5), .O3(out_10[3]),
    .O2(out_10[2]), .O1(out_10[1]), .O0(out_10[0]));
  _4_bit_Alu u_4_bit_alu_2 (
    .out_14(n4_bit_alu_2_out_14), .out_15(n4_bit_alu_2_out_15), .in_7(in_1), .A(A[7:4]), .in_8(in_2),
    .B(B[7:4]), .in_9(in_3), .Ain(Ain), .Bin(Bin), .Cin_a(n4_bit_alu_1_out_14), .Cin_s(n4_bit_alu_1_out_15),
    .O3(out_10[7]), .O2(out_10[6]), .O1(out_10[5]), .O0(out_10[4]));
  _4_bit_Alu u_4_bit_alu_3 (
    .out_14(n4_bit_alu_3_out_14), .out_15(n4_bit_alu_3_out_15), .in_7(in_1), .A(A[11:8]), .in_8(in_2),
    .B(B[11:8]), .in_9(in_3), .Ain(Ain), .Bin(Bin), .Cin_a(n4_bit_alu_2_out_14), .Cin_s(n4_bit_alu_2_out_15),
    .O3(out_10[11]), .O2(out_10[10]), .O1(out_10[9]), .O0(out_10[8]));
  _4_bit_Alu u_4_bit_alu_4 (
    .out_14(out_11), .out_15(out_12), .in_7(in_1), .A(A[15:12]), .in_8(in_2), .B(B[15:12]), .in_9(in_3),
    .Ain(Ain), .Bin(Bin), .Cin_a(n4_bit_alu_3_out_14), .Cin_s(n4_bit_alu_3_out_15), .O3(out_10[15]),
    .O2(out_10[14]), .O1(out_10[13]), .O0(out_10[12]));
endmodule

module project (
  input  [15:0] B,
  input  [15:0] A,
  input  in_3,
  input  in_4,
  input  [3:0] in_5,
  input  [7:0] MA,
  input  [7:0] MB,
  output [15:0] out_8,
  output out_9,
  output out_10,
  output [2:0] out_11
);

  wire [15:0] n8_bit_multiplier_1_out_17, n16_bit_au_1_out_6, n16bit_lu_1_out_4;

  _16_bit_AU u_16_bit_au_1 (
    .A(A), .B(B), .in_1(in_3), .out_6(n16_bit_au_1_out_6), .in_2(in_4), .in_5(out_11), .out_7(out_9),
    .out_8(out_10));
  _8_bit_multiplier u_8_bit_multiplier_1 (
    .B7(MB[7]), .B6(MB[6]), .B5(MB[5]), .B4(MB[4]), .B3(MB[3]), .B2(MB[2]), .B1(MB[1]), .B0(MB[0]),
    .A7(MA[7]), .A6(MA[6]), .A5(MA[5]), .A4(MA[4]), .A3(MA[3]), .A2(MA[2]), .A1(MA[1]), .A0(MA[0]),
    .out_17(n8_bit_multiplier_1_out_17));
  _16bit_lu u_16bit_lu_1 (.out_4(n16bit_lu_1_out_4), .B(B), .A(A), .in_3(out_11));
  Multiplexer #(.select(2), .width(16), .enable("false")) multiplexer_1 (
    .in0(n16bit_lu_1_out_4), .in1(n16_bit_au_1_out_6), .in3(n8_bit_multiplier_1_out_17), .out(out_8),
    .sel({in_5[2], in_5[3]}));  // open: in2
  // Probe on out_8
  Aluop aluop_1 (.out_5(out_11), .A(in_5[3]), .B(in_5[2]), .C(in_5[1]), .D(in_5[0]));
endmodule

module Aluop (
  input  A,
  input  B,
  input  C,
  input  D,
  output [2:0] out_5
);

  wire and_1_out, and_2_out, and_3_out, and_4_out, and_5_out, and_6_out;

  and and_1 (and_1_out, ~A, C);  // AND_Gate
  and and_2 (and_2_out, B, ~D);  // AND_Gate
  and and_3 (and_3_out, A, ~D);  // AND_Gate
  and and_4 (and_4_out, ~A, C, D);  // AND_Gate
  and and_5 (and_5_out, ~B, C, A);  // AND_Gate
  and and_6 (and_6_out, C, D);
  or or_1 (out_5[0], and_1_out, and_2_out);
  or or_2 (out_5[1], and_3_out, and_4_out);
  or or_3 (out_5[2], and_5_out, and_6_out);
endmodule

module _32_bit_project (
  input  [3:0] in_1,
  input  [31:0] B,
  input  [31:0] A,
  input  in_4,
  input  in_5,
  input  [15:0] A_2,
  input  [15:0] B_2,
  output [31:0] out_8,
  output out_9,
  output out_10,
  output [2:0] out_11
);

  wire project_1_out_9, project_1_out_10;

  // Probe on A
  project project_1 (
    .out_8(out_8[15:0]), .out_9(project_1_out_9), .out_10(project_1_out_10), .out_11(out_11), .MA(B_2[7:0]),
    .MB(A_2[7:0]), .B(B[15:0]), .A(A[15:0]), .in_3(in_4), .in_4(in_5), .in_5(in_1));
  project project_2 (
    .out_8(out_8[31:16]), .out_9(out_9), .out_10(out_10), .out_11(out_11), .MA(B_2[15:8]), .MB(A_2[15:8]),
    .B(B[31:16]), .A(A[31:16]), .in_3(project_1_out_9), .in_4(project_1_out_10), .in_5(in_1));
  // Probe on out_8
endmodule

module regis (
  input  Write_En,
  input  [3:0] RS,
  input  [3:0] RD,
  input  [15:0] in_4,
  input  [3:0] RT,
  input  Clock,
  input  Reset,
  output [15:0] data_1,
  output [15:0] data_2
);

  wire demultiplexer_1_out0, demultiplexer_1_out1, demultiplexer_1_out2, demultiplexer_1_out3,
       demultiplexer_1_out4, demultiplexer_1_out5, demultiplexer_1_out6, demultiplexer_1_out7,
       demultiplexer_1_out8, demultiplexer_1_out9, demultiplexer_1_out10, demultiplexer_1_out11,
       demultiplexer_1_out12, demultiplexer_1_out13, demultiplexer_1_out14, demultiplexer_1_out15;
  wire [15:0] register_1_q, register_2_q, register_3_q, register_4_q, register_5_q, register_6_q,
       register_7_q, register_8_q, register_9_q, register_10_q, register_11_q, register_12_q, register_13_q,
       register_14_q, register_15_q, register_16_q;

  Demultiplexer #(.select(4), .enable("false")) demultiplexer_1 (
    .out0(demultiplexer_1_out0), .out1(demultiplexer_1_out1), .out2(demultiplexer_1_out2),
    .out3(demultiplexer_1_out3), .out4(demultiplexer_1_out4), .out5(demultiplexer_1_out5),
    .out6(demultiplexer_1_out6), .out7(demultiplexer_1_out7), .out8(demultiplexer_1_out8),
    .out9(demultiplexer_1_out9), .out10(demultiplexer_1_out10), .out11(demultiplexer_1_out11),
    .out12(demultiplexer_1_out12), .out13(demultiplexer_1_out13), .out14(demultiplexer_1_out14),
    .out15(demultiplexer_1_out15), .in(Write_En), .sel(RD));
  Register #(.width(16)) register_1 (.D(in_4), .en(demultiplexer_1_out0), .Q(register_1_q), .clk(Clock), .clr(Reset));
  Register #(.width(16)) register_2 (.D(in_4), .en(demultiplexer_1_out1), .Q(register_2_q), .clk(Clock), .clr(Reset));
  Register #(.width(16)) register_3 (.D(in_4), .en(demultiplexer_1_out2), .Q(register_3_q), .clk(Clock), .clr(Reset));
  Register #(.width(16)) register_4 (.D(in_4), .en(demultiplexer_1_out3), .Q(register_4_q), .clk(Clock), .clr(Reset));
  Register #(.width(16)) register_5 (.D(in_4), .en(demultiplexer_1_out4), .Q(register_5_q), .clk(Clock), .clr(Reset));
  Register #(.width(16)) register_6 (.D(in_4), .en(demultiplexer_1_out5), .Q(register_6_q), .clk(Clock), .clr(Reset));
  Register #(.width(16)) register_7 (.D(in_4), .en(demultiplexer_1_out6), .Q(register_7_q), .clk(Clock), .clr(Reset));
  Register #(.width(16)) register_8 (.D(in_4), .en(demultiplexer_1_out7), .Q(register_8_q), .clk(Clock), .clr(Reset));
  Register #(.width(16)) register_9 (.D(in_4), .en(demultiplexer_1_out8), .Q(register_9_q), .clk(Clock), .clr(Reset));
  Register #(.width(16)) register_10 (.D(in_4), .en(demultiplexer_1_out9), .Q(register_10_q), .clk(Clock), .clr(Reset));
  Register #(.width(16)) register_11 (
    .D(in_4), .en(demultiplexer_1_out10), .Q(register_11_q), .clk(Clock), .clr(Reset));
  Register #(.width(16)) register_12 (
    .D(in_4), .en(demultiplexer_1_out11), .Q(register_12_q), .clk(Clock), .clr(Reset));
  Register #(.width(16)) register_13 (
    .D(in_4), .en(demultiplexer_1_out12), .Q(register_13_q), .clk(Clock), .clr(Reset));
  Register #(.width(16)) register_14 (
    .D(in_4), .en(demultiplexer_1_out13), .Q(register_14_q), .clk(Clock), .clr(Reset));
  Register #(.width(16)) register_15 (
    .D(in_4), .en(demultiplexer_1_out14), .Q(register_15_q), .clk(Clock), .clr(Reset));
  Register #(.width(16)) register_16 (
    .D(in_4), .en(demultiplexer_1_out15), .Q(register_16_q), .clk(Clock), .clr(Reset));
  Multiplexer #(.select(4), .width(16), .enable("false")) multiplexer_1 (
    .in0(register_1_q), .in1(register_2_q), .in2(register_3_q), .in3(register_4_q), .in4(register_5_q),
    .in5(register_6_q), .in6(register_7_q), .in7(register_8_q), .in8(register_9_q), .in9(register_10_q),
    .in10(register_11_q), .in11(register_12_q), .in12(register_13_q), .in13(register_14_q),
    .in14(register_15_q), .in15(register_16_q), .out(data_1), .sel(RS));
  Multiplexer #(.select(4), .width(16), .enable("false")) multiplexer_2 (
    .in0(register_1_q), .in1(register_2_q), .in2(register_3_q), .in3(register_4_q), .in4(register_5_q),
    .in5(register_6_q), .in6(register_7_q), .in7(register_8_q), .in8(register_9_q), .in9(register_10_q),
    .in10(register_11_q), .in11(register_12_q), .in12(register_13_q), .in13(register_14_q),
    .in14(register_15_q), .in15(register_16_q), .out(data_2), .sel(RT));
endmodule

module regs1 (
  input  in_1,
  input  [3:0] in_2,
  input  in_3,
  input  in_4,
  input  in_5,
  output [3:0] Op,
  output [3:0] RS,
  output [3:0] RT,
  output [3:0] RD
);

  wire clock_1_out;
  wire [15:0] project_1_out_8, regis_1_data_1, register_1_q;

  Register #(.width(16)) register_1 (.Q(register_1_q));  // open: D, en, clk, clr
  ROM #(.addrWidth(16), .dataWidth(16)) rom_1 (.addr(register_1_q), .data({Op, RS, RT, RD}));  // open: sel
  Clock clock_1 (.out(clock_1_out));
  regis regis_1 (
    .RD(RD), .Clock(clock_1_out), .Reset(in_1), .data_1(regis_1_data_1), .data_2(regis_1_data_1),
    .Write_En(in_5), .in_4(project_1_out_8), .RS(RS), .RT(RT));
  project project_1 (
    .out_8(project_1_out_8), .B(regis_1_data_1), .A(regis_1_data_1), .in_3(in_3), .in_5(in_2));  // open: out_9, out_10, out_11, MA, MB, in_4

  // Notes on the sheet:
  //   contents of rom_1 (hex, n*v repeats v):
  //   1459
endmodule

module lw_sw (
  input  [3:0] in_1,
  input  in_2,
  input  in_3,
  input  in_4,
  input  in_5,
  input  sw,
  input  lw,
  output [3:0] Op,
  output [15:0] rd1,
  output [15:0] rd2,
  output [3:0] RS,
  output [3:0] RT,
  output [3:0] RD
);

  wire clock_1_out;
  wire [15:0] adder_1_out, project_1_out_8, ram_1_data, regis_1_data_2, register_1_q;

  Register #(.width(16)) register_1 (.D(adder_1_out), .Q(register_1_q), .clk(clock_1_out));  // open: en, clr
  Adder #(.width(16)) adder_1 (.a(register_1_q), .b(16'h1), .out(adder_1_out));  // open: cin, cout
  ROM #(.addrWidth(16), .dataWidth(16)) rom_1 (.addr(register_1_q), .data({Op, RS, RT, RD}));  // open: sel
  Clock clock_1 (.out(clock_1_out));
  regis regis_1 (
    .RD(RT), .Clock(clock_1_out), .Reset(in_4), .data_1(rd1), .data_2(regis_1_data_2), .Write_En(in_5),
    .in_4(ram_1_data), .RS(RS), .RT(RT));
  assign rd2 = {{12{1'b0}}, RD};  // Bit_Extender bit_extender_1
  project project_1 (
    .out_8(project_1_out_8), .B(rd2), .A(rd1), .in_3(in_2), .in_4(in_3), .in_5(in_1));  // open: out_9, out_10, out_11, MA, MB
  RAM #(.addrWidth(16), .dataWidth(16), .bus("separate")) ram_1 (
    .addr(project_1_out_8), .din(regis_1_data_2), .data(ram_1_data), .str(sw), .clk(clock_1_out), .ld(lw));  // open: sel, clr

  // Notes on the sheet:
  //   contents of rom_1 (hex, n*v repeats v):
  //   456 123
endmodule

module R_type (
  input  in_1,
  input  in_2,
  input  [3:0] in_3,
  input  in_4,
  output [3:0] Op,
  output [3:0] RS,
  output [3:0] RT,
  output [3:0] RD,
  output [15:0] out_9
);

  wire clock_1_out;
  wire [15:0] adder_1_out, regis_1_data_1, regis_1_data_2, register_1_q;

  Register #(.width(16)) register_1 (.D(adder_1_out), .Q(register_1_q));  // open: en, clk, clr
  Adder #(.width(16)) adder_1 (.a(register_1_q), .b(16'h1), .out(adder_1_out));  // open: cin, cout
  ROM #(.addrWidth(16), .dataWidth(16)) rom_1 (.addr(register_1_q), .data({Op, RS, RT, RD}));  // open: sel
  Clock clock_1 (.out(clock_1_out));
  regis regis_1 (
    .RD(RD), .Clock(clock_1_out), .Reset(in_1), .data_1(regis_1_data_1), .data_2(regis_1_data_2),
    .Write_En(in_4), .in_4(out_9), .RS(RS), .RT(RT));
  project project_1 (
    .out_8(out_9), .B(regis_1_data_2), .A(regis_1_data_1), .in_3(in_2), .in_5(in_3));  // open: out_9, out_10, out_11, MA, MB, in_4

  // Notes on the sheet:
  //   contents of rom_1 (hex, n*v repeats v):
  //   123
endmodule

module I_type (
  input  [3:0] in_1,
  input  in_2,
  input  in_3,
  input  in_4,
  input  in_5,
  output [3:0] Op,
  output [15:0] rd1,
  output [15:0] rd2,
  output [3:0] RS,
  output [3:0] RT,
  output [3:0] RD,
  output [15:0] out_12
);

  wire clock_1_out;
  wire [15:0] adder_1_out, project_1_out_8, register_1_q;

  Register #(.width(16)) register_1 (.D(adder_1_out), .Q(register_1_q), .clk(clock_1_out));  // open: en, clr
  Adder #(.width(16)) adder_1 (.a(register_1_q), .b(16'h1), .out(adder_1_out));  // open: cin, cout
  ROM #(.addrWidth(16), .dataWidth(16)) rom_1 (.addr(register_1_q), .data({Op, RS, RT, RD}));  // open: sel
  Clock clock_1 (.out(clock_1_out));
  regis regis_1 (
    .RD(RT), .Clock(clock_1_out), .Reset(in_4), .data_1(rd1), .data_2(out_12), .Write_En(in_5),
    .in_4(project_1_out_8), .RS(RS), .RT(RT));
  assign rd2 = {{12{1'b0}}, RD};  // Bit_Extender bit_extender_1
  project project_1 (
    .out_8(project_1_out_8), .B(rd2), .A(rd1), .in_3(in_2), .in_4(in_3), .in_5(in_1));  // open: out_9, out_10, out_11, MA, MB

  // Notes on the sheet:
  //   contents of rom_1 (hex, n*v repeats v):
  //   123 123
endmodule

module part_2 (
  input  [3:0] in_1,
  input  in_2,
  input  in_3,
  input  in_4,
  input  in_5,
  input  in_6,
  input  in_7,
  input  in_8,
  input  in_9,
  input  in_10,
  output [3:0] Op,
  output [15:0] rd1,
  output [15:0] rd2,
  output [3:0] RS,
  output [3:0] RT,
  output [3:0] RD
);

  wire clock_1_out;
  wire [3:0] multiplexer_1_out;
  wire [7:0] bit_extender_2_out, bit_extender_3_out;
  wire [15:0] adder_1_out, bit_extender_1_out, multiplexer_3_out, project_1_out_8, ram_1_data,
       regis_1_data_2, register_1_q;

  Register #(.width(16)) register_1 (.D(adder_1_out), .Q(register_1_q), .clk(clock_1_out));  // open: en, clr
  Adder #(.width(16)) adder_1 (.a(register_1_q), .b(16'h1), .out(adder_1_out));  // open: cin, cout
  ROM #(.addrWidth(16), .dataWidth(16)) rom_1 (.addr(register_1_q), .data({Op, RS, RT, RD}));  // open: sel
  Clock clock_1 (.out(clock_1_out));
  Multiplexer #(.width(4), .enable("false")) multiplexer_1 (.in0(RT), .in1(RD), .out(multiplexer_1_out), .sel(in_5));
  regis regis_1 (
    .RD(multiplexer_1_out), .Clock(clock_1_out), .Reset(in_2), .data_1(rd1), .data_2(regis_1_data_2),
    .Write_En(in_6), .in_4(multiplexer_3_out), .RS(RS), .RT(RT));
  assign bit_extender_1_out = {{12{1'b0}}, RD};  // Bit_Extender bit_extender_1
  Bit_Extender #(.in_width(16), .out_width(8)) bit_extender_2 (.in(rd1), .out(bit_extender_2_out));
  Multiplexer #(.width(16), .enable("false")) multiplexer_2 (
    .in0(regis_1_data_2), .in1(bit_extender_1_out), .out(rd2), .sel(in_8));
  Bit_Extender #(.in_width(16), .out_width(8)) bit_extender_3 (.in(rd2), .out(bit_extender_3_out));
  project project_1 (
    .out_8(project_1_out_8), .MA(bit_extender_2_out), .MB(bit_extender_3_out), .B(rd2), .A(rd1), .in_3(in_4),
    .in_4(in_3), .in_5(in_1));  // open: out_9, out_10, out_11
  Multiplexer #(.width(16), .enable("false")) multiplexer_3 (
    .in0(project_1_out_8), .in1(ram_1_data), .out(multiplexer_3_out), .sel(in_7));
  RAM #(.addrWidth(16), .dataWidth(16), .bus("separate")) ram_1 (
    .addr(project_1_out_8), .din(regis_1_data_2), .data(ram_1_data), .str(in_10), .clk(clock_1_out), .ld(in_9));  // open: sel, clr

  // Other names for the same wires on the sheet: Ain = in_4; ALUSrc = in_8; Bin = in_3; MemRead = in_9;
  //   MemtoReg = in_7; MemWrite = in_10; RegDst = in_5; RegWrite = in_6

  // Notes on the sheet:
  //   contents of rom_1 (hex, n*v repeats v):
  //   456 123
endmodule
