// Logisim project riaz_mheadi_1931746042_.circ as structural Verilog
module _1_bit_LU (
  input  A,
  input  B,
  input  [1:0] in_3,
  output out_4
);

  wire and_1_out, not_1_out, or_1_out, xor_1_out;

  and and_1 (and_1_out, A, B);
  or or_1 (or_1_out, A, B);
  xor xor_1 (xor_1_out, A, B);
  not not_1 (not_1_out, A);
  Multiplexer #(.select(2), .enable("false")) multiplexer_1 (
    .in0(and_1_out), .in1(or_1_out), .in2(xor_1_out), .in3(not_1_out), .out(out_4), .sel(in_3));
endmodule

module _2_bit_Lu (
  input  A,
  input  B,
  input  A_2,
  input  B_2,
  input  [1:0] in_5,
  output out_6,
  output out_7
);

  wire and_1_out, and_2_out, not_1_out, not_2_out, or_1_out, or_2_out, xor_1_out, xor_2_out;

  and and_1 (and_1_out, A, B);
  or or_1 (or_1_out, A, B);
  xor xor_1 (xor_1_out, A, B);
  not not_1 (not_1_out, A);
  and and_2 (and_2_out, A_2, B_2);
  or or_2 (or_2_out, A_2, B_2);
  xor xor_2 (xor_2_out, A_2, B_2);
  not not_2 (not_2_out, A_2);
  Multiplexer #(.select(2), .enable("false")) multiplexer_1 (
    .in0(and_1_out), .in1(or_1_out), .in2(xor_1_out), .in3(not_1_out), .out(out_6), .sel(in_5));
  Multiplexer #(.select(2), .enable("false")) multiplexer_2 (
    .in0(and_2_out), .in1(or_2_out), .in2(xor_2_out), .in3(not_2_out), .out(out_7), .sel(in_5));
endmodule

module _16bit_lu (
  input  [15:0] in_1,
  input  [15:0] in_2,
  input  [1:0] in_3,
  output out_4,
  output out_5,
  output out_6,
  output out_7,
  output out_8,
  output out_9,
  output out_10,
  output out_11,
  output out_12,
  output out_13,
  output out_14,
  output out_15,
  output out_16,
  output out_17,
  output out_18,
  output out_19
);

  _4_bit_lu u_4_bit_lu_1 (
    .out_10(out_4), .out_11(out_5), .out_12(out_6), .out_13(out_7), .A(in_2[0]), .A_2(in_2[1]),
    .A_3(in_2[2]), .A_4(in_2[3]), .B(in_1[0]), .B_2(in_1[1]), .B_3(in_1[2]), .B_4(in_1[3]), .in_9(in_3));
  _4_bit_lu u_4_bit_lu_2 (
    .out_10(out_8), .out_11(out_9), .out_12(out_10), .out_13(out_11), .A(in_2[4]), .A_2(in_2[5]),
    .A_3(in_2[6]), .A_4(in_2[7]), .B(in_1[4]), .B_2(in_1[5]), .B_3(in_1[6]), .B_4(in_1[7]), .in_9(in_3));
  _4_bit_lu u_4_bit_lu_3 (
    .out_10(out_12), .out_11(out_13), .out_12(out_14), .out_13(out_15), .A(in_2[8]), .A_2(in_2[9]),
    .A_3(in_2[10]), .A_4(in_2[11]), .B(in_1[8]), .B_2(in_1[9]), .B_3(in_1[10]), .B_4(in_1[11]), .in_9(in_3));
  _4_bit_lu u_4_bit_lu_4 (
    .out_10(out_16), .out_11(out_17), .out_12(out_18), .out_13(out_19), .A(in_2[12]), .A_2(in_2[13]),
    .A_3(in_2[14]), .A_4(in_2[15]), .B(in_1[12]), .B_2(in_1[13]), .B_3(in_1[14]), .B_4(in_1[15]), .in_9(in_3));
endmodule

module Extra (
  input  [3:0] in_1,
  input  [3:0] in_2,
  input  [1:0] in_3,
  output F1,
  output F2,
  output F3,
  output F4
);

  _1_bit_LU u_1_bit_lu_1 (.in_3(in_3), .out_4(F1), .A(in_2[0]), .B(in_1[0]));
  _1_bit_LU u_1_bit_lu_2 (.in_3(in_3), .out_4(F2), .A(in_2[1]), .B(in_1[1]));
  _1_bit_LU u_1_bit_lu_3 (.in_3(in_3), .out_4(F3), .A(in_2[2]), .B(in_1[2]));
  _1_bit_LU u_1_bit_lu_4 (.in_3(in_3), .out_4(F4), .A(in_2[3]), .B(in_1[3]));
endmodule

module _4_bit_lu (
  input  A,
  input  B,
  input  A_2,
  input  B_2,
  input  A_3,
  input  B_3,
  input  A_4,
  input  B_4,
  input  [1:0] in_9,
  output out_10,
  output out_11,
  output out_12,
  output out_13
);

  wire and_1_out, and_2_out, and_3_out, and_4_out, not_1_out, not_2_out, not_3_out, not_4_out, or_1_out,
       or_2_out, or_3_out, or_4_out, xor_1_out, xor_2_out, xor_3_out, xor_4_out;

  and and_1 (and_1_out, A, B);
  or or_1 (or_1_out, A, B);
  xor xor_1 (xor_1_out, A, B);
  not not_1 (not_1_out, A);
  and and_2 (and_2_out, A_2, B_2);
  or or_2 (or_2_out, A_2, B_2);
  xor xor_2 (xor_2_out, A_2, B_2);
  not not_2 (not_2_out, A_2);
  and and_3 (and_3_out, A_3, B_3);
  or or_3 (or_3_out, A_3, B_3);
  xor xor_3 (xor_3_out, A_3, B_3);
  not not_3 (not_3_out, A_3);
  and and_4 (and_4_out, A_4, B_4);
  or or_4 (or_4_out, A_4, B_4);
  xor xor_4 (xor_4_out, A_4, B_4);
  not not_4 (not_4_out, A_4);
  Multiplexer #(.select(2), .enable("false")) multiplexer_1 (
    .in0(and_1_out), .in1(or_1_out), .in2(xor_1_out), .in3(not_1_out), .out(out_10), .sel(in_9));
  Multiplexer #(.select(2), .enable("false")) multiplexer_2 (
    .in0(and_2_out), .in1(or_2_out), .in2(xor_2_out), .in3(not_2_out), .out(out_11), .sel(in_9));
  Multiplexer #(.select(2), .enable("false")) multiplexer_3 (
    .in0(and_3_out), .in1(or_3_out), .in2(xor_3_out), .in3(not_3_out), .out(out_12), .sel(in_9));
  Multiplexer #(.select(2), .enable("false")) multiplexer_4 (
    .in0(and_4_out), .in1(or_4_out), .in2(xor_4_out), .in3(not_4_out), .out(out_13), .sel(in_9));
endmodule

module _1_bit_AU (
  input  A,
  input  B,
  input  Cin,
  input  S1,
  input  S0,
  output out_6,
  output out_7
);

  wire multiplexer_1_out, not_1_out;

  not not_1 (not_1_out, B);
  Multiplexer #(.select(2), .enable("false")) multiplexer_1 (
    .in0(B), .in1(not_1_out), .in2(1'b0), .in3(1'b1), .out(multiplexer_1_out), .sel({S1, S0}));
  _1_bit_adder u_1_bit_adder_1 (.S(out_6), .Cout(out_7), .A(A), .B(multiplexer_1_out), .Cin(Cin));
endmodule

module _1_bit_adder (
  input  A,
  input  B,
  input  Cin,
  output S,
  output Cout
);

  wire and_1_out, and_2_out, xor_1_out;

  xor xor_1 (xor_1_out, A, B);
  xor xor_2 (S, xor_1_out, Cin);
  and and_1 (and_1_out, Cin, xor_1_out);
  and and_2 (and_2_out, A, B);
  or or_1 (Cout, and_1_out, and_2_out);
endmodule

module _4_bit_Au (
  input  cin,
  input  B3,
  input  B2,
  input  B1,
  input  B0,
  input  A3,
  input  A2,
  input  A1,
  input  A0,
  input  [1:0] S1S0,
  output D3,
  output D2,
  output D1,
  output D0,
  output Cout
);

  wire n1_bit_au_1_out_7, n1_bit_au_2_out_7, n1_bit_au_3_out_7;

  _1_bit_AU u_1_bit_au_1 (.A(A0), .B(B0), .Cin(cin), .S1(S1S0[1]), .S0(S1S0[0]), .out_7(n1_bit_au_1_out_7), .out_6(D0));
  _1_bit_AU u_1_bit_au_2 (
    .A(A1), .B(B1), .Cin(n1_bit_au_1_out_7), .S1(S1S0[1]), .S0(S1S0[0]), .out_7(n1_bit_au_2_out_7), .out_6(D1));
  _1_bit_AU u_1_bit_au_3 (
    .A(A2), .B(B2), .Cin(n1_bit_au_2_out_7), .S1(S1S0[1]), .S0(S1S0[0]), .out_7(n1_bit_au_3_out_7), .out_6(D2));
  _1_bit_AU u_1_bit_au_4 (
    .A(A3), .B(B3), .Cin(n1_bit_au_3_out_7), .S1(S1S0[1]), .S0(S1S0[0]), .out_7(Cout), .out_6(D3));
endmodule

module _16_bit_AU (
  input  in_1,
  input  [15:0] A,
  input  [15:0] B,
  input  [1:0] in_4,
  output [15:0] out_5,
  output out_6
);

  wire n4_bit_au_1_cout, n4_bit_au_2_cout, n4_bit_au_3_cout;

  _4_bit_Au u_4_bit_au_1 (
    .Cout(n4_bit_au_1_cout), .B3(B[3]), .B2(B[2]), .B1(B[1]), .B0(B[0]), .A3(A[3]), .A2(A[2]), .A1(A[1]),
    .A0(A[0]), .cin(in_1), .S1S0(in_4), .D0(out_5[0]), .D1(out_5[1]), .D2(out_5[2]), .D3(out_5[3]));
  _4_bit_Au u_4_bit_au_2 (
    .Cout(n4_bit_au_2_cout), .B3(B[7]), .B2(B[6]), .B1(B[5]), .B0(B[4]), .A3(A[7]), .A2(A[6]), .A1(A[5]),
    .A0(A[4]), .cin(n4_bit_au_1_cout), .S1S0(in_4), .D0(out_5[4]), .D1(out_5[5]), .D2(out_5[6]), .D3(out_5[7]));
  _4_bit_Au u_4_bit_au_3 (
    .Cout(n4_bit_au_3_cout), .B3(A[11]), .B2(A[10]), .B1(A[9]), .B0(A[8]), .A3(B[11]), .A2(B[10]), .A1(B[9]),
    .A0(B[8]), .cin(n4_bit_au_2_cout), .S1S0(in_4), .D0(out_5[8]), .D1(out_5[9]), .D2(out_5[10]),
    .D3(out_5[11]));
  _4_bit_Au u_4_bit_au_4 (
    .Cout(out_6), .B3(A[15]), .B2(A[14]), .B1(A[13]), .B0(A[12]), .A3(B[15]), .A2(B[14]), .A1(B[13]),
    .A0(B[12]), .cin(n4_bit_au_3_cout), .S1S0(in_4), .D0(out_5[12]), .D1(out_5[13]), .D2(out_5[14]),
    .D3(out_5[15]));
endmodule

module _4_bit_adder (
  input  Cin,
  input  A3,
  input  A2,
  input  A1,
  input  A0,
  input  B3,
  input  B2,
  input  B1,
  input  B0,
  output S0,
  output S1,
  output S2,
  output S3,
  output out_14
);

  wire n1_bit_adder_1_cout, n1_bit_adder_2_cout, n1_bit_adder_3_cout;

  _1_bit_adder u_1_bit_adder_1 (.S(S0), .Cout(n1_bit_adder_1_cout), .A(A0), .B(B0), .Cin(Cin));
  _1_bit_adder u_1_bit_adder_2 (.S(S1), .Cout(n1_bit_adder_2_cout), .A(A1), .B(B1), .Cin(n1_bit_adder_1_cout));
  _1_bit_adder u_1_bit_adder_3 (.S(S2), .Cout(n1_bit_adder_3_cout), .A(A2), .B(B2), .Cin(n1_bit_adder_2_cout));
  _1_bit_adder u_1_bit_adder_4 (.S(S3), .Cout(out_14), .A(A3), .B(B3), .Cin(n1_bit_adder_3_cout));
endmodule

module _4_bit_multiplier (
  input  B3,
  input  B2,
  input  B1,
  input  B0,
  input  A3,
  input  A2,
  input  A1,
  input  A0,
  output [7:0] out_9
);

  wire and_2_out, and_3_out, and_4_out, and_5_out, and_6_out, and_7_out, and_8_out, and_9_out, and_10_out,
       and_11_out, and_12_out, and_13_out, and_14_out, and_15_out, and_16_out, n4_bit_adder_1_out_14,
       n4_bit_adder_1_s1, n4_bit_adder_1_s2, n4_bit_adder_1_s3, n4_bit_adder_2_out_14, n4_bit_adder_2_s1,
       n4_bit_adder_2_s2, n4_bit_adder_2_s3;

  and and_1 (out_9[0], B0, A0);
  and and_2 (and_2_out, B1, A0);
  and and_3 (and_3_out, B2, A0);
  and and_4 (and_4_out, B3, A0);
  and and_5 (and_5_out, B0, A1);
  and and_6 (and_6_out, B1, A1);
  and and_7 (and_7_out, B2, A1);
  and and_8 (and_8_out, B3, A1);
  and and_9 (and_9_out, B0, A2);
  and and_10 (and_10_out, B1, A2);
  and and_11 (and_11_out, B2, A2);
  and and_12 (and_12_out, B3, A2);
  and and_13 (and_13_out, B0, A3);
  and and_14 (and_14_out, B1, A3);
  and and_15 (and_15_out, B2, A3);
  and and_16 (and_16_out, B3, A3);
  _4_bit_adder u_4_bit_adder_1 (
    .out_14(n4_bit_adder_1_out_14), .Cin(1'b0), .A2(and_7_out), .A1(and_6_out), .A0(and_5_out), .B3(1'b0),
    .B2(and_4_out), .B1(and_3_out), .B0(and_2_out), .A3(and_8_out), .S0(out_9[1]), .S1(n4_bit_adder_1_s1),
    .S3(n4_bit_adder_1_s3), .S2(n4_bit_adder_1_s2));
  _4_bit_adder u_4_bit_adder_2 (
    .out_14(n4_bit_adder_2_out_14), .Cin(1'b0), .A2(and_11_out), .A1(and_10_out), .A0(and_9_out),
    .B3(n4_bit_adder_1_out_14), .B2(n4_bit_adder_1_s3), .B1(n4_bit_adder_1_s2), .B0(n4_bit_adder_1_s1),
    .A3(and_12_out), .S0(out_9[2]), .S1(n4_bit_adder_2_s1), .S3(n4_bit_adder_2_s3), .S2(n4_bit_adder_2_s2));
  _4_bit_adder u_4_bit_adder_3 (
    .out_14(out_9[7]), .Cin(1'b0), .A2(and_15_out), .A1(and_14_out), .A0(and_13_out),
    .B3(n4_bit_adder_2_out_14), .B2(n4_bit_adder_2_s3), .B1(n4_bit_adder_2_s2), .B0(n4_bit_adder_2_s1),
    .A3(and_16_out), .S0(out_9[3]), .S1(out_9[4]), .S3(out_9[6]), .S2(out_9[5]));
  // Probe on out_9
endmodule

module _8_bit_multiplier (
  input  B7,
  input  B6,
  input  B5,
  input  B4,
  input  B3,
  input  B2,
  input  B1,
  input  B0,
  input  A7,
  input  A6,
  input  A5,
  input  A4,
  input  A3,
  input  A2,
  input  A1,
  input  A0,
  output [15:0] out_17
);

  wire and_2_out, and_3_out, and_4_out, and_5_out, and_6_out, and_7_out, and_8_out, and_9_out, and_10_out,
       and_11_out, and_12_out, and_13_out, and_14_out, and_15_out, and_16_out, and_17_out, and_18_out,
       and_19_out, and_20_out, and_21_out, and_22_out, and_23_out, and_24_out, and_25_out, and_26_out,
       and_27_out, and_28_out, and_29_out, and_30_out, and_31_out, and_32_out, and_33_out, and_34_out,
       and_35_out, and_36_out, and_37_out, and_38_out, and_39_out, and_40_out, and_41_out, and_42_out,
       and_43_out, and_44_out, and_45_out, and_46_out, and_47_out, and_48_out, and_49_out, and_50_out,
       and_51_out, and_52_out, and_53_out, and_54_out, and_55_out, and_56_out, and_57_out, and_58_out,
       and_59_out, and_60_out, and_61_out, and_62_out, and_63_out, and_64_out, n8_bit_adder_1_out_19,
       n8_bit_adder_1_out_20, n8_bit_adder_1_out_21, n8_bit_adder_1_out_22, n8_bit_adder_1_out_23,
       n8_bit_adder_1_out_24, n8_bit_adder_1_out_25, n8_bit_adder_1_out_26, n8_bit_adder_2_out_19,
       n8_bit_adder_2_out_20, n8_bit_adder_2_out_21, n8_bit_adder_2_out_22, n8_bit_adder_2_out_23,
       n8_bit_adder_2_out_24, n8_bit_adder_2_out_25, n8_bit_adder_2_out_26, n8_bit_adder_3_out_19,
       n8_bit_adder_3_out_20, n8_bit_adder_3_out_21, n8_bit_adder_3_out_22, n8_bit_adder_3_out_23,
       n8_bit_adder_3_out_24, n8_bit_adder_3_out_25, n8_bit_adder_3_out_26, n8_bit_adder_4_out_19,
       n8_bit_adder_4_out_20, n8_bit_adder_4_out_21, n8_bit_adder_4_out_22, n8_bit_adder_4_out_23,
       n8_bit_adder_4_out_24, n8_bit_adder_4_out_25, n8_bit_adder_4_out_26, n8_bit_adder_5_out_19,
       n8_bit_adder_5_out_20, n8_bit_adder_5_out_21, n8_bit_adder_5_out_22, n8_bit_adder_5_out_23,
       n8_bit_adder_5_out_24, n8_bit_adder_5_out_25, n8_bit_adder_5_out_26, n8_bit_adder_7_out_19,
       n8_bit_adder_7_out_20, n8_bit_adder_7_out_21, n8_bit_adder_7_out_22, n8_bit_adder_7_out_23,
       n8_bit_adder_7_out_24, n8_bit_adder_7_out_25, n8_bit_adder_7_out_26;

  and and_1 (out_17[0], B0, A0);
  and and_2 (and_2_out, B1, A0);
  and and_3 (and_3_out, B2, A0);
  and and_4 (and_4_out, B3, A0);
  and and_5 (and_5_out, B4, A0);
  and and_6 (and_6_out, B5, A0);
  and and_7 (and_7_out, B6, A0);
  and and_8 (and_8_out, B7, A0);
  and and_9 (and_9_out, B0, A1);
  and and_10 (and_10_out, B1, A1);
  and and_11 (and_11_out, B2, A1);
  and and_12 (and_12_out, B3, A1);
  and and_13 (and_13_out, B4, A1);
  and and_14 (and_14_out, B5, A1);
  and and_15 (and_15_out, B6, A1);
  and and_16 (and_16_out, B7, A1);
  and and_17 (and_17_out, B0, A2);
  and and_18 (and_18_out, B1, A2);
  and and_19 (and_19_out, B2, A2);
  and and_20 (and_20_out, B3, A2);
  and and_21 (and_21_out, B4, A2);
  and and_22 (and_22_out, B5, A2);
  and and_23 (and_23_out, B6, A2);
  and and_24 (and_24_out, B7, A2);
  and and_25 (and_25_out, B0, A3);
  and and_26 (and_26_out, B1, A3);
  and and_27 (and_27_out, B2, A3);
  and and_28 (and_28_out, B3, A3);
  and and_29 (and_29_out, B4, A3);
  and and_30 (and_30_out, B5, A3);
  and and_31 (and_31_out, B6, A3);
  and and_32 (and_32_out, B7, A3);
  and and_33 (and_33_out, B0, A4);
  and and_34 (and_34_out, B1, A4);
  and and_35 (and_35_out, B2, A4);
  and and_36 (and_36_out, B3, A4);
  and and_37 (and_37_out, B4, A4);
  and and_38 (and_38_out, B5, A4);
  and and_39 (and_39_out, B6, A4);
  and and_40 (and_40_out, B7, A4);
  and and_41 (and_41_out, B0, A5);
  and and_42 (and_42_out, B1, A5);
  and and_43 (and_43_out, B2, A5);
  and and_44 (and_44_out, B3, A5);
  and and_45 (and_45_out, B4, A5);
  and and_46 (and_46_out, B5, A5);
  and and_47 (and_47_out, B6, A5);
  and and_48 (and_48_out, B7, A5);
  and and_49 (and_49_out, B0, A6);
  and and_50 (and_50_out, B1, A6);
  and and_51 (and_51_out, B2, A6);
  and and_52 (and_52_out, B3, A6);
  and and_53 (and_53_out, B4, A6);
  and and_54 (and_54_out, B5, A6);
  and and_55 (and_55_out, B6, A6);
  and and_56 (and_56_out, B7, A6);
  and and_57 (and_57_out, B0, A7);
  and and_58 (and_58_out, B1, A7);
  and and_59 (and_59_out, B2, A7);
  and and_60 (and_60_out, B3, A7);
  and and_61 (and_61_out, B4, A7);
  and and_62 (and_62_out, B5, A7);
  and and_63 (and_63_out, B6, A7);
  and and_64 (and_64_out, B7, A7);
  _8_bit_adder u_8_bit_adder_1 (
    .out_18(out_17[1]), .out_19(n8_bit_adder_1_out_19), .out_20(n8_bit_adder_1_out_20),
    .out_21(n8_bit_adder_1_out_21), .out_22(n8_bit_adder_1_out_22), .out_23(n8_bit_adder_1_out_23),
    .out_24(n8_bit_adder_1_out_24), .out_25(n8_bit_adder_1_out_25), .out_26(n8_bit_adder_1_out_26),
    .B7(and_16_out), .B6(and_15_out), .B5(and_14_out), .B4(and_13_out), .B3(and_12_out), .B2(and_11_out),
    .B1(and_10_out), .B0(and_9_out), .A7(1'b0), .A6(and_8_out), .A5(and_7_out), .A4(and_6_out),
    .A3(and_5_out), .A2(and_4_out), .A1(and_3_out), .A0(and_2_out), .Cin(1'b0));
  _8_bit_adder u_8_bit_adder_2 (
    .out_18(out_17[3]), .out_19(n8_bit_adder_2_out_19), .out_20(n8_bit_adder_2_out_20),
    .out_21(n8_bit_adder_2_out_21), .out_22(n8_bit_adder_2_out_22), .out_23(n8_bit_adder_2_out_23),
    .out_24(n8_bit_adder_2_out_24), .out_25(n8_bit_adder_2_out_25), .out_26(n8_bit_adder_2_out_26),
    .B7(and_32_out), .B6(and_31_out), .B5(and_30_out), .B4(and_29_out), .B3(and_28_out), .B2(and_27_out),
    .B1(and_26_out), .B0(and_25_out), .A7(n8_bit_adder_7_out_26), .A6(n8_bit_adder_7_out_25),
    .A5(n8_bit_adder_7_out_24), .A4(n8_bit_adder_7_out_23), .A3(n8_bit_adder_7_out_22),
    .A2(n8_bit_adder_7_out_21), .A1(n8_bit_adder_7_out_20), .A0(n8_bit_adder_7_out_19), .Cin(1'b0));
  _8_bit_adder u_8_bit_adder_3 (
    .out_18(out_17[4]), .out_19(n8_bit_adder_3_out_19), .out_20(n8_bit_adder_3_out_20),
    .out_21(n8_bit_adder_3_out_21), .out_22(n8_bit_adder_3_out_22), .out_23(n8_bit_adder_3_out_23),
    .out_24(n8_bit_adder_3_out_24), .out_25(n8_bit_adder_3_out_25), .out_26(n8_bit_adder_3_out_26),
    .B7(and_40_out), .B6(and_39_out), .B5(and_38_out), .B4(and_37_out), .B3(and_36_out), .B2(and_35_out),
    .B1(and_34_out), .B0(and_33_out), .A7(n8_bit_adder_2_out_26), .A6(n8_bit_adder_2_out_25),
    .A5(n8_bit_adder_2_out_24), .A4(n8_bit_adder_2_out_23), .A3(n8_bit_adder_2_out_22),
    .A2(n8_bit_adder_2_out_21), .A1(n8_bit_adder_2_out_20), .A0(n8_bit_adder_2_out_19), .Cin(1'b0));
  _8_bit_adder u_8_bit_adder_4 (
    .out_18(out_17[5]), .out_19(n8_bit_adder_4_out_19), .out_20(n8_bit_adder_4_out_20),
    .out_21(n8_bit_adder_4_out_21), .out_22(n8_bit_adder_4_out_22), .out_23(n8_bit_adder_4_out_23),
    .out_24(n8_bit_adder_4_out_24), .out_25(n8_bit_adder_4_out_25), .out_26(n8_bit_adder_4_out_26),
    .B7(and_48_out), .B6(and_47_out), .B5(and_46_out), .B4(and_45_out), .B3(and_44_out), .B2(and_43_out),
    .B1(and_42_out), .B0(and_41_out), .A7(n8_bit_adder_3_out_26), .A6(n8_bit_adder_3_out_25),
    .A5(n8_bit_adder_3_out_24), .A4(n8_bit_adder_3_out_23), .A3(n8_bit_adder_3_out_22),
    .A2(n8_bit_adder_3_out_21), .A1(n8_bit_adder_3_out_20), .A0(n8_bit_adder_3_out_19), .Cin(1'b0));
  _8_bit_adder u_8_bit_adder_5 (
    .out_18(out_17[6]), .out_19(n8_bit_adder_5_out_19), .out_20(n8_bit_adder_5_out_20),
    .out_21(n8_bit_adder_5_out_21), .out_22(n8_bit_adder_5_out_22), .out_23(n8_bit_adder_5_out_23),
    .out_24(n8_bit_adder_5_out_24), .out_25(n8_bit_adder_5_out_25), .out_26(n8_bit_adder_5_out_26),
    .B7(and_56_out), .B6(and_55_out), .B5(and_54_out), .B4(and_53_out), .B3(and_52_out), .B2(and_51_out),
    .B1(and_50_out), .B0(and_49_out), .A7(n8_bit_adder_4_out_26), .A6(n8_bit_adder_4_out_25),
    .A5(n8_bit_adder_4_out_24), .A4(n8_bit_adder_4_out_23), .A3(n8_bit_adder_4_out_22),
    .A2(n8_bit_adder_4_out_21), .A1(n8_bit_adder_4_out_20), .A0(n8_bit_adder_4_out_19), .Cin(1'b0));
  _8_bit_adder u_8_bit_adder_6 (
    .out_18(out_17[7]), .out_19(out_17[8]), .out_20(out_17[9]), .out_21(out_17[10]), .out_22(out_17[11]),
    .out_23(out_17[12]), .out_24(out_17[13]), .out_25(out_17[14]), .out_26(out_17[15]), .B7(and_64_out),
    .B6(and_63_out), .B5(and_62_out), .B4(and_61_out), .B3(and_60_out), .B2(and_59_out), .B1(and_58_out),
    .B0(and_57_out), .A7(n8_bit_adder_5_out_26), .A6(n8_bit_adder_5_out_25), .A5(n8_bit_adder_5_out_24),
    .A4(n8_bit_adder_5_out_23), .A3(n8_bit_adder_5_out_22), .A2(n8_bit_adder_5_out_21),
    .A1(n8_bit_adder_5_out_20), .A0(n8_bit_adder_5_out_19), .Cin(1'b0));
  _8_bit_adder u_8_bit_adder_7 (
    .out_18(out_17[2]), .out_19(n8_bit_adder_7_out_19), .out_20(n8_bit_adder_7_out_20),
    .out_21(n8_bit_adder_7_out_21), .out_22(n8_bit_adder_7_out_22), .out_23(n8_bit_adder_7_out_23),
    .out_24(n8_bit_adder_7_out_24), .out_25(n8_bit_adder_7_out_25), .out_26(n8_bit_adder_7_out_26),
    .B7(and_24_out), .B6(and_23_out), .B5(and_22_out), .B4(and_21_out), .B3(and_20_out), .B2(and_19_out),
    .B1(and_18_out), .B0(and_17_out), .A7(n8_bit_adder_1_out_26), .A6(n8_bit_adder_1_out_25),
    .A5(n8_bit_adder_1_out_24), .A4(n8_bit_adder_1_out_23), .A3(n8_bit_adder_1_out_22),
    .A2(n8_bit_adder_1_out_21), .A1(n8_bit_adder_1_out_20), .A0(n8_bit_adder_1_out_19), .Cin(1'b0));
  // Probe on out_17
endmodule

module _8_bit_adder (
  input  B7,
  input  B6,
  input  B5,
  input  B4,
  input  B3,
  input  B2,
  input  B1,
  input  B0,
  input  A7,
  input  A6,
  input  A5,
  input  A4,
  input  A3,
  input  A2,
  input  A1,
  input  A0,
  input  Cin,
  output out_18,
  output out_19,
  output out_20,
  output out_21,
  output out_22,
  output out_23,
  output out_24,
  output out_25,
  output out_26
);

  wire n4_bit_adder_1_out_14;

  _4_bit_adder u_4_bit_adder_1 (
    .out_14(n4_bit_adder_1_out_14), .Cin(Cin), .A2(A2), .A1(A1), .A0(A0), .B3(B3), .B2(B2), .B1(B1), .B0(B0),
    .A3(A3), .S0(out_18), .S1(out_19), .S3(out_21), .S2(out_20));
  _4_bit_adder u_4_bit_adder_2 (
    .out_14(out_26), .Cin(n4_bit_adder_1_out_14), .A2(A6), .A1(A5), .A0(A4), .B3(B7), .B2(B6), .B1(B5),
    .B0(B4), .A3(A7), .S0(out_22), .S1(out_23), .S3(out_25), .S2(out_24));
endmodule

module _1_bit_Alu (
  input  A,
  input  B,
  input  Ain,
  input  Bin,
  input  Cin_add,
  input  Cin_sub,
  input  [2:0] in_7,
  output out_8,
  output Cout_add,
  output Cout_Sub
);

  wire and_1_out, comparator_1_lt, multiplexer_1_out, multiplexer_2_out, multiplier_1_out, n1_bit_adder_1_s,
       n1_bit_adder_2_s, not_1_out, not_2_out, or_1_out;

  not not_1 (not_1_out, A);
  Multiplexer #(.enable("false")) multiplexer_1 (.in0(B), .in1(not_2_out), .out(multiplexer_1_out), .sel(Bin));
  not not_2 (not_2_out, B);
  Multiplexer #(.enable("false")) multiplexer_2 (.in0(A), .in1(not_1_out), .out(multiplexer_2_out), .sel(Ain));
  and and_1 (and_1_out, multiplexer_2_out, multiplexer_1_out);
  or or_1 (or_1_out, multiplexer_2_out, multiplexer_1_out);
  Multiplier #(.width(1)) multiplier_1 (
    .a(multiplexer_2_out), .b(multiplexer_1_out), .out(multiplier_1_out));  // open: cin, cout
  Comparator #(.width(1)) comparator_1 (
    .a(multiplexer_2_out), .b(multiplexer_1_out), .lt(comparator_1_lt));  // open: gt, eq
  _1_bit_adder u_1_bit_adder_1 (
    .S(n1_bit_adder_1_s), .Cout(Cout_add), .A(multiplexer_2_out), .B(multiplexer_1_out), .Cin(Cin_add));
  _1_bit_adder u_1_bit_adder_2 (
    .S(n1_bit_adder_2_s), .Cout(Cout_Sub), .A(multiplexer_2_out), .B(multiplexer_1_out), .Cin(Cin_sub));
  Multiplexer #(.select(3), .enable("false")) multiplexer_3 (
    .in0(and_1_out), .in1(or_1_out), .in2(n1_bit_adder_1_s), .in3(multiplier_1_out), .in6(n1_bit_adder_2_s),
    .in7(comparator_1_lt), .out(out_8), .sel(in_7));  // open: in4, in5
endmodule

module Alu_con_in (
  input  F5,
  input  F4,
  input  F3,
  input  F2,
  input  F1,
  input  F0,
  input  OP0,
  input  OP1,
  output [2:0] out_9
);

  wire and_1_out, or_1_out;

  or or_1 (or_1_out, F3, F0);
  and and_1 (and_1_out, OP1, F1);
  and and_2 (out_9[2], OP1, or_1_out);
  // AND_Gate and_3 has open pins: in0=OP0, in1=OP0, out=open
  or or_2 (out_9[0], OP0, and_1_out);
  or or_3 (out_9[1], ~OP1, ~F2);  // OR_Gate
endmodule

module _4_bit_Alu (
  input  [3:0] A,
  input  [3:0] B,
  input  Ain,
  input  Bin,
  input  Cin_a,
  input  Cin_s,
  input  [5:0] in_7,
  input  in_8,
  input  in_9,
  output O3,
  output O2,
  output O1,
  output O0,
  output out_14,
  output out_15,
  output [2:0] out_16
);

  wire n1_bit_alu_1_cout_add, n1_bit_alu_1_cout_sub, n1_bit_alu_2_cout_add, n1_bit_alu_2_cout_sub,
       n1_bit_alu_3_cout_add, n1_bit_alu_3_cout_sub;

  Alu_con_in alu_con_in_1 (
    .out_9(out_16), .F5(in_7[5]), .F4(in_7[4]), .F3(in_7[3]), .F2(in_7[2]), .F1(in_7[1]), .F0(in_7[0]),
    .OP0(in_9), .OP1(in_8));
  _1_bit_Alu u_1_bit_alu_1 (
    .A(A[0]), .B(B[0]), .Ain(Ain), .Bin(Bin), .Cin_add(Cin_a), .Cin_sub(Cin_s), .out_8(O0),
    .Cout_add(n1_bit_alu_1_cout_add), .Cout_Sub(n1_bit_alu_1_cout_sub), .in_7(out_16));
  _1_bit_Alu u_1_bit_alu_2 (
    .A(A[1]), .B(B[1]), .Ain(Ain), .Bin(Bin), .Cin_add(n1_bit_alu_1_cout_add),
    .Cin_sub(n1_bit_alu_1_cout_sub), .out_8(O1), .Cout_add(n1_bit_alu_2_cout_add),
    .Cout_Sub(n1_bit_alu_2_cout_sub), .in_7(out_16));
  _1_bit_Alu u_1_bit_alu_3 (
    .A(A[2]), .B(B[2]), .Ain(Ain), .Bin(Bin), .Cin_add(n1_bit_alu_2_cout_add),
    .Cin_sub(n1_bit_alu_2_cout_sub), .out_8(O2), .Cout_add(n1_bit_alu_3_cout_add),
    .Cout_Sub(n1_bit_alu_3_cout_sub), .in_7(out_16));
  _1_bit_Alu u_1_bit_alu_4 (
    .A(A[3]), .B(B[3]), .Ain(Ain), .Bin(Bin), .Cin_add(n1_bit_alu_3_cout_add),
    .Cin_sub(n1_bit_alu_3_cout_sub), .out_8(O3), .Cout_add(out_14), .Cout_Sub(out_15), .in_7(out_16));
endmodule

module _1_bit_mid_Alu (
  input  A,
  input  B,
  input  in_3,
  input  [2:0] in_4,
  output out_5,
  output Cout_add
);

  wire and_1_out, n1_bit_adder_1_s, nand_1_out, nor_1_out, not_1_out, or_1_out, xor_1_out;

  xor xor_1 (xor_1_out, A, B);
  not not_1 (not_1_out, A);
  nand nand_1 (nand_1_out, A, B);
  nor nor_1 (nor_1_out, A, B);
  or or_1 (or_1_out, A, B);
  and and_1 (and_1_out, A, B);
  _1_bit_adder u_1_bit_adder_1 (.S(n1_bit_adder_1_s), .Cout(Cout_add), .A(B), .B(A), .Cin(in_3));
  Multiplexer #(.select(3), .enable("false")) multiplexer_1 (
    .in0(xor_1_out), .in1(not_1_out), .in2(nand_1_out), .in3(nor_1_out), .in4(n1_bit_adder_1_s),
    .in5(or_1_out), .in6(and_1_out), .out(out_5), .sel(in_4));  // open: in7
endmodule

module _4_bit_alu_mid (
  input  cin,
  input  B3,
  input  B2,
  input  B1,
  input  B0,
  input  A3,
  input  A2,
  input  A1,
  input  A0,
  input  [2:0] in_10,
  output D3,
  output D2,
  output D1,
  output D0,
  output Cout
);

  wire n1_bit_mid_alu_1_cout_add, n1_bit_mid_alu_2_cout_add, n1_bit_mid_alu_3_cout_add;

  _1_bit_mid_Alu u_1_bit_mid_alu_1 (
    .out_5(D0), .Cout_add(n1_bit_mid_alu_1_cout_add), .A(A0), .B(B0), .in_3(cin), .in_4(in_10));
  _1_bit_mid_Alu u_1_bit_mid_alu_2 (
    .out_5(D1), .Cout_add(n1_bit_mid_alu_2_cout_add), .A(A1), .B(B1), .in_3(n1_bit_mid_alu_1_cout_add),
    .in_4(in_10));
  _1_bit_mid_Alu u_1_bit_mid_alu_3 (
    .out_5(D2), .Cout_add(n1_bit_mid_alu_3_cout_add), .A(A2), .B(B2), .in_3(n1_bit_mid_alu_2_cout_add),
    .in_4(in_10));
  _1_bit_mid_Alu u_1_bit_mid_alu_4 (
    .out_5(D3), .Cout_add(Cout), .A(A3), .B(B3), .in_3(n1_bit_mid_alu_3_cout_add), .in_4(in_10));
endmodule

module _3_bit_multi_mid (
  input  B3,
  input  B1,
  input  B0,
  input  A3,
  input  A1,
  input  A0,
  input  in_7,
  output [5:0] out_8,
  output out_9
);

  wire and_2_out, and_3_out, and_4_out, and_5_out, and_6_out, and_7_out, and_8_out, and_9_out,
       n4_bit_adder_1_out_14, n4_bit_adder_1_s1, n4_bit_adder_1_s2, n4_bit_adder_1_s3;

  and and_1 (out_8[0], B0, A0);
  and and_2 (and_2_out, B1, A0);
  and and_3 (and_3_out, B3, A0);
  and and_4 (and_4_out, B0, A1);
  and and_5 (and_5_out, B1, A1);
  and and_6 (and_6_out, B3, A1);
  and and_7 (and_7_out, B0, A3);
  and and_8 (and_8_out, B1, A3);
  and and_9 (and_9_out, B3, A3);
  _4_bit_adder u_4_bit_adder_1 (
    .out_14(n4_bit_adder_1_out_14), .Cin(in_7), .A2(and_6_out), .A1(and_5_out), .A0(and_4_out), .B3(1'b0),
    .B2(1'b0), .B1(and_3_out), .B0(and_2_out), .A3(1'b0), .S0(out_8[1]), .S1(n4_bit_adder_1_s1),
    .S3(n4_bit_adder_1_s3), .S2(n4_bit_adder_1_s2));
  _4_bit_adder u_4_bit_adder_2 (
    .out_14(out_9), .Cin(1'b0), .A2(and_9_out), .A1(and_8_out), .A0(and_7_out), .B3(n4_bit_adder_1_out_14),
    .B2(n4_bit_adder_1_s3), .B1(n4_bit_adder_1_s2), .B0(n4_bit_adder_1_s1), .A3(1'b0), .S0(out_8[2]),
    .S1(out_8[3]), .S3(out_8[5]), .S2(out_8[4]));
  // Probe on out_8
endmodule
