// Logisim project riaz_mheadi_1931746042_task1.circ as structural Verilog
module _1_bit_LU (
  input  A,
  input  B,
  input  [1:0] in_3,
  output out_4
);

  wire and_1_out, not_1_out, or_1_out, xor_1_out;

  and and_1 (and_1_out, A, B);
  or or_1 (or_1_out, A, B);
  xor xor_1 (xor_1_out, A, B);
  not not_1 (not_1_out, A);
  Multiplexer #(.select(2), .enable("false")) multiplexer_1 (
    .in0(and_1_out), .in1(or_1_out), .in2(xor_1_out), .in3(not_1_out), .out(out_4), .sel(in_3));
endmodule

module _2_bit_Lu (
  input  A,
  input  B,
  input  A_2,
  input  B_2,
  input  [1:0] in_5,
  output out_6,
  output out_7
);

  wire and_1_out, and_2_out, not_1_out, not_2_out, or_1_out, or_2_out, xor_1_out, xor_2_out;

  and and_1 (and_1_out, A, B);
  or or_1 (or_1_out, A, B);
  xor xor_1 (xor_1_out, A, B);
  not not_1 (not_1_out, A);
  and and_2 (and_2_out, A_2, B_2);
  or or_2 (or_2_out, A_2, B_2);
  xor xor_2 (xor_2_out, A_2, B_2);
  not not_2 (not_2_out, A_2);
  Multiplexer #(.select(2), .enable("false")) multiplexer_1 (
    .in0(and_1_out), .in1(or_1_out), .in2(xor_1_out), .in3(not_1_out), .out(out_6), .sel(in_5));
  Multiplexer #(.select(2), .enable("false")) multiplexer_2 (
    .in0(and_2_out), .in1(or_2_out), .in2(xor_2_out), .in3(not_2_out), .out(out_7), .sel(in_5));
endmodule

module _16bit_lu (
  input  [15:0] in_1,
  input  [15:0] in_2,
  input  [1:0] in_3,
  output out_4,
  output out_5,
  output out_6,
  output out_7,
  output out_8,
  output out_9,
  output out_10,
  output out_11,
  output out_12,
  output out_13,
  output out_14,
  output out_15,
  output out_16,
  output out_17,
  output out_18,
  output out_19
);

  _4_bit_lu u_4_bit_lu_1 (
    .out_10(out_4), .out_11(out_5), .out_12(out_6), .out_13(out_7), .A(in_2[0]), .A_2(in_2[1]),
    .A_3(in_2[2]), .A_4(in_2[3]), .B(in_1[0]), .B_2(in_1[1]), .B_3(in_1[2]), .B_4(in_1[3]), .in_9(in_3));
  _4_bit_lu u_4_bit_lu_2 (
    .out_10(out_8), .out_11(out_9), .out_12(out_10), .out_13(out_11), .A(in_2[4]), .A_2(in_2[5]),
    .A_3(in_2[6]), .A_4(in_2[7]), .B(in_1[4]), .B_2(in_1[5]), .B_3(in_1[6]), .B_4(in_1[7]), .in_9(in_3));
  _4_bit_lu u_4_bit_lu_3 (
    .out_10(out_12), .out_11(out_13), .out_12(out_14), .out_13(out_15), .A(in_2[8]), .A_2(in_2[9]),
    .A_3(in_2[10]), .A_4(in_2[11]), .B(in_1[8]), .B_2(in_1[9]), .B_3(in_1[10]), .B_4(in_1[11]), .in_9(in_3));
  _4_bit_lu u_4_bit_lu_4 (
    .out_10(out_16), .out_11(out_17), .out_12(out_18), .out_13(out_19), .A(in_2[12]), .A_2(in_2[13]),
    .A_3(in_2[14]), .A_4(in_2[15]), .B(in_1[12]), .B_2(in_1[13]), .B_3(in_1[14]), .B_4(in_1[15]), .in_9(in_3));
endmodule

module Extra (
  input  [3:0] in_1,
  input  [3:0] in_2,
  input  [1:0] in_3,
  output F1,
  output F2,
  output F3,
  output F4
);

  _1_bit_LU u_1_bit_lu_1 (.in_3(in_3), .out_4(F1), .A(in_2[0]), .B(in_1[0]));
  _1_bit_LU u_1_bit_lu_2 (.in_3(in_3), .out_4(F2), .A(in_2[1]), .B(in_1[1]));
  _1_bit_LU u_1_bit_lu_3 (.in_3(in_3), .out_4(F3), .A(in_2[2]), .B(in_1[2]));
  _1_bit_LU u_1_bit_lu_4 (.in_3(in_3), .out_4(F4), .A(in_2[3]), .B(in_1[3]));
endmodule

module _4_bit_lu (
  input  A,
  input  B,
  input  A_2,
  input  B_2,
  input  A_3,
  input  B_3,
  input  A_4,
  input  B_4,
  input  [1:0] in_9,
  output out_10,
  output out_11,
  output out_12,
  output out_13
);

  wire and_1_out, and_2_out, and_3_out, and_4_out, not_1_out, not_2_out, not_3_out, not_4_out, or_1_out,
       or_2_out, or_3_out, or_4_out, xor_1_out, xor_2_out, xor_3_out, xor_4_out;

  and and_1 (and_1_out, A, B);
  or or_1 (or_1_out, A, B);
  xor xor_1 (xor_1_out, A, B);
  not not_1 (not_1_out, A);
  and and_2 (and_2_out, A_2, B_2);
  or or_2 (or_2_out, A_2, B_2);
  xor xor_2 (xor_2_out, A_2, B_2);
  not not_2 (not_2_out, A_2);
  and and_3 (and_3_out, A_3, B_3);
  or or_3 (or_3_out, A_3, B_3);
  xor xor_3 (xor_3_out, A_3, B_3);
  not not_3 (not_3_out, A_3);
  and and_4 (and_4_out, A_4, B_4);
  or or_4 (or_4_out, A_4, B_4);
  xor xor_4 (xor_4_out, A_4, B_4);
  not not_4 (not_4_out, A_4);
  Multiplexer #(.select(2), .enable("false")) multiplexer_1 (
    .in0(and_1_out), .in1(or_1_out), .in2(xor_1_out), .in3(not_1_out), .out(out_10), .sel(in_9));
  Multiplexer #(.select(2), .enable("false")) multiplexer_2 (
    .in0(and_2_out), .in1(or_2_out), .in2(xor_2_out), .in3(not_2_out), .out(out_11), .sel(in_9));
  Multiplexer #(.select(2), .enable("false")) multiplexer_3 (
    .in0(and_3_out), .in1(or_3_out), .in2(xor_3_out), .in3(not_3_out), .out(out_12), .sel(in_9));
  Multiplexer #(.select(2), .enable("false")) multiplexer_4 (
    .in0(and_4_out), .in1(or_4_out), .in2(xor_4_out), .in3(not_4_out), .out(out_13), .sel(in_9));
endmodule
